// Digital circuit MIPS32CPU.dig as structural Verilog
module MIPS32CPU (
  input  CLK,
  input  reset,
  output invpc,
  output iAddr,
  output [31:0] t_0,
  output [31:0] t_1,
  output [31:0] t_2
);

  wire ALUsrc, and_1_out, and_2_out, branch, branche, immS, isZ, jump, memread, memwrite, not_1_out,
       or_1_out, RegDst, regwrite;
  wire [1:0] memtoReg;
  wire [2:0] ALUop, opcontrol;
  wire [4:0] multiplexer_4_out;
  wire [5:0] func;
  wire [9:0] u_pcdecoder_ppc, u_shift_out;
  wire [10:0] u_memoryDecoder_paddr;
  wire [15:6] i_15_0;
  wire [31:0] multiplexer_1_out, multiplexer_2_out, multiplexer_5_out, multiplexer_6_out, next_pc,
       pc_plus_4_s, PC_q, rwd, SignEx_out, u_alu_r, u_BranchTarget_out, u_datamemory_rdata, u_JumpTarget_out,
       u_lui_res, u_regfile_da, u_regfile_db, u_zeroExtension_res;
  wire [31:16] Ins;

  Multiplexer #(.Bits(32)) multiplexer_1 (.sel(reset), .in_0(next_pc), .in_1(32'h400000), .out(multiplexer_1_out));
  Register #(.Bits(32)) PC (.D(multiplexer_1_out), .C(CLK), .en(1'b1), .Q(PC_q));
  pcdecoder #(.applicationType("IVERILOG")) u_pcdecoder (.vpc(PC_q), .ppc(u_pcdecoder_ppc), .invpc(invpc));
  Add #(.Bits(32)) pc_plus_4 (.a(PC_q), .b(32'h4), .c_i(1'b0), .s(pc_plus_4_s));  // open: c_o
  // Probe on {Ins[25:16], i_15_0, func}
  JumpTarget #(.applicationType("IVERILOG")) u_JumpTarget (
    .in({Ins[25:16], i_15_0, func}), .pc4(pc_plus_4_s), .out(u_JumpTarget_out));
  BranchTarget #(.applicationType("IVERILOG")) u_BranchTarget (
    .imm({i_15_0, func}), .pc4(pc_plus_4_s), .out(u_BranchTarget_out));
  shift #(.applicationType("IVERILOG")) u_shift (.in(u_pcdecoder_ppc), .out(u_shift_out));
  Multiplexer #(.Bits(32)) multiplexer_2 (
    .sel(or_1_out), .in_0(pc_plus_4_s), .in_1(u_BranchTarget_out), .out(multiplexer_2_out));
  // Probe on pc_plus_4_s
  // Probe on u_JumpTarget_out
  Multiplexer #(.Bits(32)) multiplexer_3 (.sel(jump), .in_0(multiplexer_2_out), .in_1(u_JumpTarget_out), .out(next_pc));
  ROM #(.AddrBits(10), .Bits(32)) Ins_mem (.A(u_shift_out), .sel(1'b1), .D({Ins, i_15_0, func}));
  // Mips32Dasm mips32dasm_1: pin names not known; wires that end beside it: {Ins, i_15_0, func}, {Ins, i_15_0, func}
  controlunit #(.applicationType("IVERILOG")) u_controlunit (
    .opcode(Ins[31:26]), .RegDst(RegDst), .branch(branch), .memread(memread), .memwrite(memwrite),
    .memtoReg(memtoReg), .ALUop(ALUop), .Alusrc(ALUsrc), .regwrite(regwrite), .jump(jump), .bne(branche),
    .immS(immS));
  or or_1 (or_1_out, and_1_out, and_2_out);
  and and_1 (and_1_out, isZ, branch);
  and and_2 (and_2_out, branche, not_1_out);
  not not_1 (not_1_out, isZ);
  alucontrol #(.applicationType("IVERILOG")) u_alucontrol (.aluop(ALUop), .func(func), .op(opcontrol));
  Multiplexer #(.Bits(5)) multiplexer_4 (
    .sel(RegDst), .in_0(Ins[20:16]), .in_1(i_15_0[15:11]), .out(multiplexer_4_out));
  // Probe on rwd
  BitExtender #(.inputBits(16), .outputBits(32)) SignEx (.in({i_15_0, func}), .out(SignEx_out));
  zeroExtension #(.applicationType("IVERILOG")) u_zeroExtension (.n({i_15_0, func}), .res(u_zeroExtension_res));
  regfile #(.applicationType("IVERILOG")) u_regfile (
    .clk(CLK), .Ra(Ins[25:21]), .Rb(Ins[20:16]), .Rw(multiplexer_4_out), .we(regwrite), .din(rwd),
    .Da(u_regfile_da), .Db(u_regfile_db), .t_0(t_0), .t_1(t_1), .t_2(t_2));
  Multiplexer #(.Bits(32)) multiplexer_5 (
    .sel(immS), .in_0(SignEx_out), .in_1(u_zeroExtension_res), .out(multiplexer_5_out));
  // Probe on u_regfile_db
  // Probe on u_regfile_da
  Multiplexer #(.Bits(32)) multiplexer_6 (
    .sel(ALUsrc), .in_0(u_regfile_db), .in_1(multiplexer_5_out), .out(multiplexer_6_out));
  alu #(.applicationType("IVERILOG")) u_alu (
    .a(u_regfile_da), .b(multiplexer_6_out), .op(opcontrol), .r(u_alu_r), .isZ(isZ));
  lui #(.applicationType("IVERILOG")) u_lui (.n({i_15_0, func}), .res(u_lui_res));
  memoryDecoder #(.applicationType("IVERILOG")) u_memoryDecoder (
    .vAddr(u_alu_r), .pAddr(u_memoryDecoder_paddr), .iAddr(iAddr));
  Multiplexer #(.Selector_Bits(2), .Bits(32)) multiplexer_7 (
    .sel(memtoReg), .in_0(u_alu_r), .in_1(u_datamemory_rdata), .in_2(u_lui_res), .in_3({32{1'b0}}), .out(rwd));
  // Probe on memtoReg
  // Probe on rwd
  datamemory #(.applicationType("IVERILOG")) u_datamemory (
    .clk(CLK), .addr(u_memoryDecoder_paddr), .wData(u_regfile_db), .mwrite(memread), .mread(memwrite),
    .rdata(u_datamemory_rdata));

  // Other names for the same wires on the sheet: i_15_0[5:0] = func; Ins[15:0] = {i_15_0, func};
  //   sa[4:0] = i_15_0[10:6]; rd[4:0] = i_15_0[15:11]; rt[4:0] = Ins[20:16]; rs[4:0] = Ins[25:21];
  //   op[5:0] = Ins[31:26]

  // Notes on the sheet:
  //   contents of Ins_mem (hex, n*v repeats v):
  //   3c08aabb,3c09ccdd,3c0a1122,8100003
endmodule

/* Test case:
CLK t_0         t_1          t_2	reset
0   x		x	     x		1
1   x		x	     x		0
0   x		x	     x		0
C   0xaabb0000  x            x  	0
C   0xaabb0000  0xccdd0000   x		0
C   0xaabb0000  0xccdd0000   0x11220000 0
*/

/* Code of pcdecoder:
module pcdecoder(
    input [31:0] vpc,
    output reg[9:0] ppc,
    output reg invpc
);

parameter [31:0] startp=32'h400000 ;
parameter [31:0] endp=32'h401000 ;

always @(*)
begin
    if(vpc>=startp 
    & vpc<endp)begin
            ppc = vpc - startp;
	    invpc = 1'b0;
    end else begin
        invpc = 1'b1;
        ppc = 7'dx;
    end
end
endmodule
*/

/* Code of JumpTarget:
module JumpTarget(
	input [25:0] in,
	input [31:0] pc4,
	output [31:0] out 
);

assign out = {pc4[31:28], in, 2'b0};

endmodule
*/

/* Code of BranchTarget:
module BranchTarget(
	input [15:0] imm,
	input [31:0] pc4,
	output [31:0] out
);

wire [31:0] signExt;

assign signExt = {{16{imm[15]}}, imm};

assign out = {signExt[29:0], 2'b0} + pc4;

endmodule
*/

/* Code of shift:
module shift(
	input [9:0] in,
	output [9:0] out
);

assign out = in >> 2;

endmodule
*/

/* Code of controlunit:
module controlunit(
    input [5:0] opcode,
    output reg RegDst,
    output reg branch,
    output reg memread,
    output reg memwrite,
    output reg [1:0]memtoReg,
    output reg [2:0]ALUop,
    output reg Alusrc,
    output reg regwrite,
    output reg jump,
    output reg bne,
    output reg immS
);

always @(*)
begin
    case (opcode)
      6'd0://R-Format((add,sub,and,or,slt)
            {RegDst,Alusrc,memtoReg,regwrite,memread,memwrite,branch,ALUop,jump,bne,immS} = {1'b1,1'b0,2'b00,1'b1,1'b0,1'b0,1'b0,3'b010,1'b0,1'b0,1'b0};
      6'd2://Jump
            {RegDst,Alusrc,memtoReg,regwrite,memread,memwrite,branch,ALUop,jump,bne,immS} = {1'b0,1'b0,2'b00,1'b0,1'b0,1'b0,1'b0,3'b000,1'b1,1'b0,1'b0};
      6'd4://beq
            {RegDst,Alusrc,memtoReg,regwrite,memread,memwrite,branch,ALUop,jump,bne,immS} = {1'b0,1'b0,2'b00,1'b0,1'b0,1'b0,1'b1,3'b001,1'b0,1'b0,1'b0};
      6'd5://bne
            {RegDst,Alusrc,memtoReg,regwrite,memread,memwrite,branch,ALUop,jump,bne,immS} = {1'b0,1'b0,2'b00,1'b0,1'b0,1'b0,1'b0,3'b001,1'b0,1'b1,1'b0};
      6'd8://addi
            {RegDst,Alusrc,memtoReg,regwrite,memread,memwrite,branch,ALUop,jump,bne,immS} = {1'b0,1'b1,2'b00,1'b1,1'b0,1'b0,1'b0,3'b000,1'b0,1'b0,1'b0};
      6'd9://addiu
            {RegDst,Alusrc,memtoReg,regwrite,memread,memwrite,branch,ALUop,jump,bne,immS} = {1'b0,1'b1,2'b00,1'b1,1'b0,1'b0,1'b0,3'b000,1'b0,1'b0,1'b0};
      6'd12://andi
            {RegDst,Alusrc,memtoReg,regwrite,memread,memwrite,branch,ALUop,jump,bne,immS} = {1'b0,1'b1,2'b00,1'b1,1'b0,1'b0,1'b0,3'b011,1'b0,1'b0,1'b1};
      6'd13://ori
            {RegDst,Alusrc,memtoReg,regwrite,memread,memwrite,branch,ALUop,jump,bne,immS} = {1'b0,1'b1,2'b00,1'b1,1'b0,1'b0,1'b0,3'b100,1'b0,1'b0,1'b1};
      6'd15://lui
            {RegDst,Alusrc,memtoReg,regwrite,memread,memwrite,branch,ALUop,jump,bne,immS} = {1'b0,1'b0,2'b10,1'b1,1'b0,1'b0,1'b0,3'b000,1'b0,1'b0,1'b0};
      6'd35://load
            {RegDst,Alusrc,memtoReg,regwrite,memread,memwrite,branch,ALUop,jump,bne,immS} = {1'b0,1'b1,2'b01,1'b1,1'b1,1'b0,1'b0,3'b000,1'b0,1'b0,1'b0};
      6'd43://store
            {RegDst,Alusrc,memtoReg,regwrite,memread,memwrite,branch,ALUop,jump,bne,immS} = {1'b0,1'b1,2'b00,1'b0,1'b0,1'b1,1'b0,3'b000,1'b0,1'b0,1'b0};

      default: 
            {RegDst,Alusrc,memtoReg,regwrite,memread,memwrite,branch,ALUop,jump,bne} = {1'bx,1'bx,2'bxx,1'bx,1'bx,1'bx,1'bx,3'bxxx,1'bx,1'bx,1'bx};
    endcase
end

endmodule
*/

/* Code of alucontrol:
module alucontrol(
    input [2:0] aluop,
    input [5:0] func,
    output reg[2:0] op
);


always @(*)
begin
    case (aluop)
      3'b000:
            op = 3'd0;//suma para lw y sw
      3'b001:
            op = 3'd1;//resta para el beq

      3'b010://R-Format
            case (func)
                6'b100000:
                        op = 3'd0;//suma 
                6'b100001:
                        op = 3'd0;//addu
                6'b100010:
                        op = 3'd1;//resta
                6'b100011:
                        op= 3'd1;//subu
                6'b100100:
                        op = 3'd2;//AND
                6'b100101:
                        op = 3'd3;//OR
                6'b101010:
                        op = 3'd4;//set less than
            default: 
                        op = 3'dx;
            endcase
        
        3'b011://and
                op = 3'd2;

        3'b100://or
                op = 3'd3;
      default:
            op = 3'dx; 
    endcase
end

endmodule
*/

/* Code of zeroExtension:
module zeroExtension(
    input [15:0] n,
    output [31:0] res
);

assign res = {16'b0,n};

endmodule
*/

/* Code of regfile:
module regfile(
input clk,
input [4:0]Ra,
input [4:0]Rb,
input [4:0]Rw,
input we,
input [31:0]din,
output reg [31:0]Da,
output reg [31:0]Db,
output [31:0] t_0,
output [31:0] t_1,
output [31:0] t_2
);

reg [31:0] memory[31:0];
assign t_0 = memory[8];
assign t_1 = memory[9];
assign t_2 = memory[10];

//seteando registros
initial $readmemh("/home/alexander/Documents/MIPS32SOC-Part2/tests/hex/RegFile.mif", memory);

always @(posedge clk)
begin
    if(we)
        memory[Rw]<=din;
    

end

always @(*)
begin
  
    
    Da<=memory[Ra];
    Db<=memory[Rb];
end
endmodule
*/

/* Code of alu:
module alu(
	input[31:0] a,
	input[31:0] b,
	input[2:0] op,
	output reg[31:0] r,
	output isZ
);

assign isZ = r == 32'd0;

always@(*)
begin
	case(op)
		3'd0: r = a + b;
		3'd1: r = a - b;
		3'd2: r = a & b;
		3'd3: r = a | b;
		3'd4: r = {31'd0, $signed(a) < $signed(b)};
		default: r = 32'dX;
	endcase
end

endmodule
*/

/* Code of lui:
module lui(
    input [15:0] n,
    output [31:0] res
);


assign res = {n,16'b0};

endmodule
*/

/* Code of memoryDecoder:
module memoryDecoder(
    input [31:0] vAddr,
    output reg [10:0] pAddr,
    output reg iAddr
);

parameter [31:0] startg=32'h10010000;
parameter [31:0] endg=32'h10011000;
parameter [31:0] starts=32'h7FFFEFFC;
parameter [31:0] ends=32'h7FFFFFFC;
parameter [31:0] sum = 32'd1024;
reg [31:0] temp;

always @(*)
begin
    if(vAddr>= startg & vAddr<endg)begin
        temp = vAddr - startg;
	pAddr = temp;
        iAddr = 1'b0;
    end else if(vAddr >= starts & vAddr<ends)begin
	temp= vAddr - starts;
     	pAddr = temp;
        iAddr = 1'b0;
    end else begin
        pAddr = 10'd0;
        iAddr = 1'b1;
    end
end

endmodule
*/

/* Code of datamemory:
module datamemory(
    input clk,
    input [10:0]addr,
    input [31:0]wData,
    input mwrite,
    input mread,
    output reg[31:0]rdata
); 

parameter [31:0] startg=32'd0 ;
parameter [31:0] endg=32'd1023 ;
parameter [31:0] starts=32'd1024 ;
parameter [31:0] ends=32'd2047 ;

reg [1023:0] stack[31:0];
reg [1023:0] global[31:0];

always @(posedge clk)
begin
    if(mwrite)
        if(addr >=startg & addr <=endg)begin
        global[addr]<=wData;
        end
        else if(addr >=startg & addr <=endg)begin
            stack[addr]<=wData;
        end

end

always @(*)
begin
    if(mread)
        if(addr >=startg & addr <=endg)begin
        rdata<=global[addr];
        end
        else if(addr >=startg & addr <=endg)begin
            rdata<=stack[addr];
        end
    	
end

endmodule
*/
