// Digital circuit MIPS32CPU.dig as structural Verilog
module MIPS32CPU (
  input  CLK,
  input  reset,
  output invpc,
  output iAddr,
  output [31:0] t_0,
  output [31:0] t_1,
  output [31:0] t_2,
  output [10:0] error,
  output iOp,
  output [31:0] w_0,
  output [31:0] t_3
);

  wire ALUsrc, and_1_out, and_2_out, branch, branche, btX, datamEn, immS, IOEn, isZ, jump, memread, memwrite,
       not_1_out, or_1_out, RegDst, regwrite, u_cpustop_stop, VGAEn;
  wire [1:0] dS, mB, memtoReg, offs;
  wire [2:0] ALUop, opcontrol;
  wire [3:0] u_MemoryWDataEncoder_owe;
  wire [4:0] multiplexer_5_out;
  wire [5:0] func;
  wire [9:0] u_pcdecoder_ppc, u_shift_out;
  wire [10:0] dmAddr, IOAddr, VGAAddr;
  wire [12:2] phyAddr;
  wire [15:6] i_15_0;
  wire [31:0] DMrd, multiplexer_1_out, multiplexer_2_out, multiplexer_3_out, multiplexer_6_out,
       multiplexer_7_out, multiplexer_9_out, next_pc, pc_plus_4_s, PC_q, rwd, SignEx_out, u_alu_r,
       u_BranchTarget_out, u_JumpTarget_out, u_lui_res, u_MemoryRDataDecoder_od, u_MemoryWDataEncoder_od,
       u_regfile_da, u_regfile_db, u_zeroExtension_res, VGArd;
  wire [31:16] Ins;

  cpustop #(.applicationType("IVERILOG")) u_cpustop (.ipc(invpc), .iAd(iAddr), .iOp(iOp), .stop(u_cpustop_stop));
  Multiplexer #(.Bits(32)) multiplexer_1 (
    .sel(reset), .in_0(multiplexer_2_out), .in_1(32'h400000), .out(multiplexer_1_out));
  Multiplexer #(.Bits(32)) multiplexer_2 (
    .sel(u_cpustop_stop), .in_0(next_pc), .in_1({32{1'b0}}), .out(multiplexer_2_out));
  Register #(.Bits(32)) PC (.D(multiplexer_1_out), .C(CLK), .en(1'b1), .Q(PC_q));
  pcdecoder #(.applicationType("IVERILOG")) u_pcdecoder (.vpc(PC_q), .ppc(u_pcdecoder_ppc), .invpc(invpc));
  Add #(.Bits(32)) pc_plus_4 (.a(PC_q), .b(32'h4), .c_i(1'b0), .s(pc_plus_4_s));  // open: c_o
  // Probe on {Ins[25:16], i_15_0, func}
  JumpTarget #(.applicationType("IVERILOG")) u_JumpTarget (
    .in({Ins[25:16], i_15_0, func}), .pc4(pc_plus_4_s), .out(u_JumpTarget_out));
  BranchTarget #(.applicationType("IVERILOG")) u_BranchTarget (
    .imm({i_15_0, func}), .pc4(pc_plus_4_s), .out(u_BranchTarget_out));
  shift #(.applicationType("IVERILOG")) u_shift (.in(u_pcdecoder_ppc), .out(u_shift_out));
  ROM #(.AddrBits(10), .Bits(32)) Ins_mem (.A(u_shift_out), .sel(1'b1), .D({Ins, i_15_0, func}));
  Multiplexer #(.Bits(32)) multiplexer_3 (
    .sel(or_1_out), .in_0(pc_plus_4_s), .in_1(u_BranchTarget_out), .out(multiplexer_3_out));
  // Mips32Dasm mips32dasm_1: pin names not known; wires that end beside it: {Ins, i_15_0, func}, {Ins, i_15_0, func}
  // Probe on pc_plus_4_s
  // Probe on u_JumpTarget_out
  Multiplexer #(.Bits(32)) multiplexer_4 (.sel(jump), .in_0(multiplexer_3_out), .in_1(u_JumpTarget_out), .out(next_pc));
  and and_1 (and_1_out, isZ, branch);
  controlunit #(.applicationType("IVERILOG")) u_controlunit (
    .opcode(Ins[31:26]), .RegDst(RegDst), .branch(branch), .memread(memread), .memwrite(memwrite),
    .memtoReg(memtoReg), .ALUop(ALUop), .Alusrc(ALUsrc), .regwrite(regwrite), .jump(jump), .bne(branche),
    .immS(immS), .dS(dS), .btX(btX), .iOp(iOp));
  or or_1 (or_1_out, and_1_out, and_2_out);
  and and_2 (and_2_out, branche, not_1_out);
  not not_1 (not_1_out, isZ);
  alucontrol #(.applicationType("IVERILOG")) u_alucontrol (.aluop(ALUop), .func(func), .op(opcontrol));
  Multiplexer #(.Bits(5)) multiplexer_5 (
    .sel(RegDst), .in_0(Ins[20:16]), .in_1(i_15_0[15:11]), .out(multiplexer_5_out));
  BitExtender #(.inputBits(16), .outputBits(32)) SignEx (.in({i_15_0, func}), .out(SignEx_out));
  zeroExtension #(.applicationType("IVERILOG")) u_zeroExtension (.n({i_15_0, func}), .res(u_zeroExtension_res));
  // Probe on rwd
  regfile #(.applicationType("IVERILOG")) u_regfile (
    .clk(CLK), .Ra(Ins[25:21]), .Rb(Ins[20:16]), .Rw(multiplexer_5_out), .we(regwrite), .din(rwd),
    .Da(u_regfile_da), .Db(u_regfile_db), .t_0(t_0), .t_1(t_1), .t_2(t_2), .t_3(t_3));
  Multiplexer #(.Bits(32)) multiplexer_6 (
    .sel(immS), .in_0(SignEx_out), .in_1(u_zeroExtension_res), .out(multiplexer_6_out));
  // Probe on u_regfile_db
  // Probe on u_regfile_da
  Multiplexer #(.Bits(32)) multiplexer_7 (
    .sel(ALUsrc), .in_0(u_regfile_db), .in_1(multiplexer_6_out), .out(multiplexer_7_out));
  Demultiplexer #(.Selector_Bits(2), .Bits(11)) demultiplexer_1 (
    .sel(mB), .in(phyAddr), .out_0(dmAddr), .out_1(VGAAddr), .out_2(IOAddr), .out_3(error));
  alu #(.applicationType("IVERILOG")) u_alu (
    .a(u_regfile_da), .b(multiplexer_7_out), .op(opcontrol), .r(u_alu_r), .isZ(isZ));
  lui #(.applicationType("IVERILOG")) u_lui (.n({i_15_0, func}), .res(u_lui_res));
  memoryDecoder #(.applicationType("IVERILOG")) u_memoryDecoder (
    .vAddr(u_alu_r), .mW(memwrite), .mR(memread), .pAd({phyAddr, offs}), .mE({IOEn, VGAEn, datamEn}),
    .mB(mB), .iAd(iAddr));
  MemoryWDataEncoder #(.applicationType("IVERILOG")) u_MemoryWDataEncoder (
    .inD(u_regfile_db), .ofs(offs), .iwe(memwrite), .ds(dS), .oD(u_MemoryWDataEncoder_od),
    .owe(u_MemoryWDataEncoder_owe));
  Multiplexer #(.Selector_Bits(2), .Bits(32)) multiplexer_8 (
    .sel(memtoReg), .in_0(u_alu_r), .in_1(u_MemoryRDataDecoder_od), .in_2(u_lui_res), .in_3({32{1'b0}}),
    .out(rwd));
  // Probe on memtoReg
  // Probe on rwd
  DataMem #(.applicationType("IVERILOG")) u_DataMem (
    .clk(CLK), .en(datamEn), .we(u_MemoryWDataEncoder_owe), .addr(dmAddr), .wd(u_MemoryWDataEncoder_od),
    .rd(DMrd), .w(w_0));
  DataMemVGA #(.applicationType("IVERILOG")) u_DataMemVGA (
    .clk(CLK), .en(VGAEn), .we(u_MemoryWDataEncoder_owe), .addr(VGAAddr), .wd(u_MemoryWDataEncoder_od),
    .rd(VGArd));
  Multiplexer #(.Selector_Bits(2), .Bits(32)) multiplexer_9 (
    .sel(mB), .in_0(DMrd), .in_1(VGArd), .in_2({32{1'b0}}), .in_3({32{1'b0}}), .out(multiplexer_9_out));
  MemoryRDataDecoder #(.applicationType("IVERILOG")) u_MemoryRDataDecoder (
    .inD(multiplexer_9_out), .ofs(offs), .bitX(btX), .ds(dS), .oD(u_MemoryRDataDecoder_od));

  // Other names for the same wires on the sheet: i_15_0[5:0] = func; Ins[15:0] = {i_15_0, func};
  //   sa[4:0] = i_15_0[10:6]; rd[4:0] = i_15_0[15:11]; rt[4:0] = Ins[20:16]; rs[4:0] = Ins[25:21];
  //   op[5:0] = Ins[31:26]; phyAddr[1:0] = offs

  // Notes on the sheet:
  //   contents of Ins_mem (hex, n*v repeats v):
  //   3c101001,26100000,3408aabb,3409ccdd,a6080000,a6090002,8100006
endmodule

/* Code of cpustop:
module cpustop(
    input ipc,
    input iAd,
    input iOp,
    output reg stop
);

always @(*)
if(ipc | iAd | iOp) begin
  stop = 1'b1;
end else begin
  stop = 1'b0;
end

endmodule
*/

/* Code of pcdecoder:
module pcdecoder(
    input [31:0] vpc,
    output reg[9:0] ppc,
    output reg invpc
);

parameter [31:0] startp=32'h400000 ;
parameter [31:0] endp=32'h401000 ;

always @(*)
begin
    if(vpc>=startp 
    & vpc<endp)begin
            ppc = vpc - startp;
	    invpc = 1'b0;
    end else begin
        invpc = 1'b1;
        ppc = 7'dx;
    end
end
endmodule
*/

/* Test case:
CLK t_0  t_1        t_2        t_3        w_0	reset
0   x    x          x          x          x       1
1   x    x          x          x          x       1
0   x    x          x          x          x       0
C   x      x          x          x          x	0
C   x      x          x          x          x	0
C   0xaabb x          x          x          x	0
C   0xaabb 0xccdd     x          x          x	0
C   0xaabb 0xccdd     x          x          0xaabb0000	0
C   0xaabb 0xccdd     x          x          0xaabbccdd	0
C   0xaabb 0xccdd     x          x          0xaabbccdd	0
*/

/* Code of JumpTarget:
module JumpTarget(
	input [25:0] in,
	input [31:0] pc4,
	output [31:0] out 
);

assign out = {pc4[31:28], in, 2'b0};

endmodule
*/

/* Code of BranchTarget:
module BranchTarget(
	input [15:0] imm,
	input [31:0] pc4,
	output [31:0] out
);

wire [31:0] signExt;

assign signExt = {{16{imm[15]}}, imm};

assign out = {signExt[29:0], 2'b0} + pc4;

endmodule
*/

/* Code of shift:
module shift(
	input [9:0] in,
	output [9:0] out
);

assign out = in >> 2;

endmodule
*/

/* Code of controlunit:
module controlunit(
    input [5:0] opcode,
    output reg RegDst,
    output reg branch,
    output reg memread,
    output reg memwrite,
    output reg [1:0]memtoReg,
    output reg [2:0]ALUop,
    output reg Alusrc,
    output reg regwrite,
    output reg jump,
    output reg bne,
    output reg immS,
    output reg [1:0]dS,
    output reg btX,
    output reg iOp
);

always @(*)
begin
    case (opcode)
      6'd0://R-Format((add,sub,and,or,slt)
      begin
            {RegDst,Alusrc,memtoReg,regwrite,memread,memwrite,branch,ALUop,jump,bne,immS} = {1'b1,1'b0,2'b00,1'b1,1'b0,1'b0,1'b0,3'b010,1'b0,1'b0,1'b0};
            dS=2'b00;
            btX=1'b0;
            iOp = 1'b0;
      end
      6'd2://Jump
      begin
            {RegDst,Alusrc,memtoReg,regwrite,memread,memwrite,branch,ALUop,jump,bne,immS} = {1'b0,1'b0,2'b00,1'b0,1'b0,1'b0,1'b0,3'b000,1'b1,1'b0,1'b0};
            dS=2'b00;
            btX=1'b0;
            iOp = 1'b0;
      end
      6'd4://beq
      begin
            {RegDst,Alusrc,memtoReg,regwrite,memread,memwrite,branch,ALUop,jump,bne,immS} = {1'b0,1'b0,2'b00,1'b0,1'b0,1'b0,1'b1,3'b001,1'b0,1'b0,1'b0};
            dS=2'b00;
            btX=1'b0;
            iOp = 1'b0;
      end
      6'd5://bne
      begin
            {RegDst,Alusrc,memtoReg,regwrite,memread,memwrite,branch,ALUop,jump,bne,immS} = {1'b0,1'b0,2'b00,1'b0,1'b0,1'b0,1'b0,3'b001,1'b0,1'b1,1'b0};
            dS=2'b00;
            btX=1'b0;
            iOp = 1'b0;
      end
      6'd8://addi
      begin
            {RegDst,Alusrc,memtoReg,regwrite,memread,memwrite,branch,ALUop,jump,bne,immS} = {1'b0,1'b1,2'b00,1'b1,1'b0,1'b0,1'b0,3'b000,1'b0,1'b0,1'b0};
            dS=2'b00;
            btX=1'b0;
            iOp = 1'b0;
      end
      6'd9://addiu
      begin
            {RegDst,Alusrc,memtoReg,regwrite,memread,memwrite,branch,ALUop,jump,bne,immS} = {1'b0,1'b1,2'b00,1'b1,1'b0,1'b0,1'b0,3'b000,1'b0,1'b0,1'b0};
            dS=2'b00;
            btX=1'b0;
            iOp = 1'b0;
      end
      6'd12://andi
      begin
            {RegDst,Alusrc,memtoReg,regwrite,memread,memwrite,branch,ALUop,jump,bne,immS} = {1'b0,1'b1,2'b00,1'b1,1'b0,1'b0,1'b0,3'b011,1'b0,1'b0,1'b1};
            dS=2'b00;
            btX=1'b0;
            iOp = 1'b0;
      end
      6'd13://ori
      begin
            {RegDst,Alusrc,memtoReg,regwrite,memread,memwrite,branch,ALUop,jump,bne,immS} = {1'b0,1'b1,2'b00,1'b1,1'b0,1'b0,1'b0,3'b100,1'b0,1'b0,1'b1};
            dS=2'b00;dS=2'b00;
            btX=1'b0;
            iOp = 1'b0;
            btX=1'b0;
            iOp = 1'b0;
      end
      6'd15://lui
      begin
            {RegDst,Alusrc,memtoReg,regwrite,memread,memwrite,branch,ALUop,jump,bne,immS} = {1'b0,1'b0,2'b10,1'b1,1'b0,1'b0,1'b0,3'b000,1'b0,1'b0,1'b0};
            dS=2'b00;
            btX=1'b0;
            iOp = 1'b0;
      end
      6'd32://lb
      begin
            {RegDst,Alusrc,memtoReg,regwrite,memread,memwrite,branch,ALUop,jump,bne,immS} 
          = {1'b0,   1'b1,  2'b01,   1'b1,    1'b1,   1'b0,    1'b0,3'b000, 1'b0,1'b0,1'b0};
            dS=2'b10;//0-Word,1-HWord,2-byte
            btX=1'b1;//1-SignEx,2-ZeroEx
            iOp = 1'b0;
      end
      6'd33://lh
      begin
            {RegDst,Alusrc,memtoReg,regwrite,memread,memwrite,branch,ALUop,jump,bne,immS} 
          = {1'b0,   1'b1,  2'b01,   1'b1,    1'b1,   1'b0,    1'b0,3'b000, 1'b0,1'b0,1'b0};
            dS=2'b01;//0-Word,1-HWord,2-byte
            btX=1'b1;//1-SignEx,2-ZeroEx
            iOp = 1'b0;
      end
      6'd35://loadword
      begin
            {RegDst,Alusrc,memtoReg,regwrite,memread,memwrite,branch,ALUop,jump,bne,immS} 
          = {1'b0,  1'b1,  2'b01,   1'b1,    1'b1,   1'b0,    1'b0,  3'b000,1'b0,1'b0,1'b0};
            dS=2'b00;//0-Word,1-HWord,2-byte
            btX=1'b1;//1-SignEx,2-ZeroEx
            iOp = 1'b0;
      end

      6'd36://lbu
      begin
            {RegDst,Alusrc,memtoReg,regwrite,memread,memwrite,branch,ALUop,jump,bne,immS} 
          = {1'b0,   1'b1,  2'b01,   1'b1,    1'b1,   1'b0,    1'b0,3'b000, 1'b0,1'b0,1'b0};
            dS=2'b10;//0-Word,1-HWord,2-byte
            btX=1'b0;//1-SignEx,2-ZeroEx
            iOp = 1'b0;
      end
      6'd37://lhu
      begin
            {RegDst,Alusrc,memtoReg,regwrite,memread,memwrite,branch,ALUop,jump,bne,immS} 
          = {1'b0,   1'b1,  2'b01,   1'b1,    1'b1,   1'b0,    1'b0,3'b000, 1'b0,1'b0,1'b0};
            dS=2'b01;//0-Word,1-HWord,2-byte
            btX=1'b0;//1-SignEx,2-ZeroEx
            iOp = 1'b0;
      end
      6'd40://sb
      begin
            {RegDst,Alusrc,memtoReg,regwrite,memread,memwrite,branch,ALUop,jump,bne,immS} 
          = {1'b0,   1'b1,  2'b00,   1'b0,    1'b0,   1'b1,    1'b0,3'b000, 1'b0,1'b0,1'b0};
            dS=2'b10;//0-Word,1-HWord,2-byte
            btX=1'b0;//1-SignEx,2-ZeroEx
            iOp = 1'b0;
      end
      6'd41://sh
      begin
            {RegDst,Alusrc,memtoReg,regwrite,memread,memwrite,branch,ALUop,jump,bne,immS} 
          = {1'b0,   1'b1,  2'b00,   1'b0,    1'b0,   1'b1,    1'b0,3'b000, 1'b0,1'b0,1'b0};
            dS=2'b01;//0-Word,1-HWord,2-byte
            btX=1'b0;//1-SignEx,2-ZeroEx
            iOp = 1'b0;
      end
      6'd43://storeword
      begin
            {RegDst,Alusrc,memtoReg,regwrite,memread,memwrite,branch,ALUop,jump,bne,immS}
          = {1'b0,  1'b1,  2'b00,   1'b0,    1'b0,   1'b1,    1'b0,  3'b000,1'b0,1'b0,1'b0};
            dS=2'b00;//0-Word,1-HWord,2-byte
            btX=1'b0;//1-SignEx,2-ZeroEx
            iOp = 1'b0;
      end
      default: 
      begin
        {RegDst,Alusrc,memtoReg,regwrite,memread,memwrite,branch,ALUop,jump,bne} = {1'bx,1'bx,2'bxx,1'bx,1'bx,1'bx,1'bx,3'bxxx,1'bx,1'bx,1'bx};
        dS=2'b00;
        btX=1'b0;
        iOp = 1'b1;
      end
            
    endcase
end

endmodule
*/

/* Code of alucontrol:
module alucontrol(
    input [2:0] aluop,
    input [5:0] func,
    output reg[2:0] op
);


always @(*)
begin
    case (aluop)
      3'b000:
            op = 3'd0;//suma para lw y sw
      3'b001:
            op = 3'd1;//resta para el beq

      3'b010://R-Format
            case (func)
                6'b100000:
                        op = 3'd0;//suma 
                6'b100001:
                        op = 3'd0;//addu
                6'b100010:
                        op = 3'd1;//resta
                6'b100011:
                        op= 3'd1;//subu
                6'b100100:
                        op = 3'd2;//AND
                6'b100101:
                        op = 3'd3;//OR
                6'b101010:
                        op = 3'd4;//set less than
            default: 
                        op = 3'dx;
            endcase
        
        3'b011://and
                op = 3'd2;

        3'b100://or
                op = 3'd3;
      default:
            op = 3'dx; 
    endcase
end

endmodule
*/

/* Code of zeroExtension:
module zeroExtension(
    input [15:0] n,
    output [31:0] res
);

assign res = {16'b0,n};

endmodule
*/

/* Code of regfile:
module regfile(
input clk,
input [4:0]Ra,
input [4:0]Rb,
input [4:0]Rw,
input we,
input [31:0]din,
output reg [31:0]Da,
output reg [31:0]Db,
output [31:0] t_0,
output [31:0] t_1,
output [31:0] t_2,
output [31:0] t_3

);

reg [31:0] memory[31:0];
assign t_0 = memory[8];
assign t_1 = memory[9];
assign t_2 = memory[10];
assign t_3 = memory[11];

//seteando registros
//initial $readmemh("/home/alexander/Documents/MIPS32SOC-Part2/tests/hex/RegFile.mif", memory);
initial begin
memory[0] = 32'b0;
end

always @(posedge clk)
begin
    if(we)
        memory[Rw]<=din;
    

end

always @(*)
begin
  
    
    Da<=memory[Ra];
    Db<=memory[Rb];
end
endmodule
*/

/* Code of alu:
module alu(
	input[31:0] a,
	input[31:0] b,
	input[2:0] op,
	output reg[31:0] r,
	output isZ
);

assign isZ = r == 32'd0;

always@(*)
begin
	case(op)
		3'd0: r = a + b;
		3'd1: r = a - b;
		3'd2: r = a & b;
		3'd3: r = a | b;
		3'd4: r = {31'd0, $signed(a) < $signed(b)};
		default: r = 32'dX;
	endcase
end

endmodule
*/

/* Code of lui:
module lui(
    input [15:0] n,
    output [31:0] res
);


assign res = {n,16'b0};

endmodule
*/

/* Code of memoryDecoder:
module memoryDecoder(
    input [31:0] vAddr,
    input mW,
    input mR,
    output reg [12:0] pAd,
    output reg[2:0] mE,
    output reg[1:0] mB,
    output reg iAd
);

parameter [31:0] startg=32'h10010000;
parameter [31:0] endg=32'h10011000;
parameter [31:0] starts=32'h7FFFEFFC;
parameter [31:0] ends=32'h7FFFFFFC;
parameter [31:0] startvga=32'hb800;
parameter [31:0] endvga = 32'hcabf;
parameter [31:0] startio = 32'hffff0000;
parameter [31:0] endio = 32'hffff000f;
reg [31:0] temp;

always @(*)

if(mW | mR) 
begin
    if(vAddr>= startg & vAddr<endg)begin
        temp = vAddr - 32'h10010000;
	    pAd = temp;
        iAd = 1'b0;
        mE = 3'b001; //enable datamemory
        mB = 2'b00; //accediendo datamemory
    end else if(vAddr >= starts & vAddr<ends)begin
	temp= vAddr - 32'h7fffdffc;
     	pAd = temp;
        iAd = 1'b0;
        mE = 3'b001;//enable data memory
        mB = 2'b00;//accediendo datamemory
    end else if(vAddr>=startvga & vAddr<=endvga)begin
        temp = vAddr - 32'hb800;
        pAd = temp;
        iAd = 1'b0;
        mE = 3'b010;//enable vga
        mB = 2'b01;//accediendo vga
    end else if(vAddr>=startio & vAddr<=endio)begin
        temp = vAddr - 32'hFFFF0000;
        pAd = temp;
        iAd = 1'b0;
        mE = 3'b100;//enable I/O
        mB = 2'b10;//accediendio I/O
    end else begin
        pAd = 13'd0;
        iAd = 1'b1;
        mE = 3'b000;
        mB = 2'b00;
    end
end

endmodule
*/

/* Code of MemoryWDataEncoder:
module MemoryWDataEncoder(
    input [31:0] inD,
    input [1:0]ofs,
    input iwe,
    input [1:0] ds,
    output reg[31:0] oD,
    output reg[3:0] owe
);

always @(*)
if(iwe)
begin
  case (ds)
        2'b00: //Word
        begin
            owe=4'b1111;
            oD = inD;
        end
        2'b01: //Half-Word
        begin
            case (ofs)
              2'b00:
              begin
                owe=4'b0011;
                oD=inD<<16;
              end
              2'b01:
              begin
                owe=4'b0011;
                oD=inD<<16;
              end
              2'b10:
              begin
                owe=4'b1100;
                oD={16'b0,inD[15:0]};
              end
              2'b11:
              begin
                owe=4'b1100;
                oD={16'b0,inD[15:0]};
              end
            endcase
        end
        2'b10: //Byte
        begin
            case(ofs)
              2'b00:
              begin
                owe=4'b0001;
                oD=inD<<24;
              end
              2'b01:
              begin
                owe=4'b0010;
                oD={8'b0,inD[7:0],16'b0};
              end
              2'b10:
              begin
                owe=4'b0100;
                oD={16'b0,inD[7:0],8'b0};
              end
              2'b11:
              begin
                owe=4'b1000;
                oD={24'b0,inD[7:0]};
              end
            endcase
        end
    default: 
        begin
        owe=4'bx;
        oD=31'bx;
        end
  endcase
end else begin
    owe=4'b0000;
    oD=31'b0;
end

endmodule
*/

/* Code of DataMem:
module DataMem(
    input clk, //! Clock input
    input en, //! Enable
    input [3:0] we, //! Per byte write enable
    input [10:0] addr, //! Address
    input [31:0] wd, //! Write data
    output [31:0] rd, //! Read data
    output [31:0] w
);
 
    reg [31:0] memory[0:2047];
    assign w = memory[0];
    assign rd = en? memory[addr] : 32'hz;


    always @(posedge clk)
    begin
        if (en) begin
            if (we[3]) memory[addr][7:0] <= wd[7:0];
            if (we[2]) memory[addr][15:8] <= wd[15:8];
            if (we[1]) memory[addr][23:16] <= wd[23:16];
            if (we[0]) memory[addr][31:24] <= wd[31:24];
        end
    end
 
`ifndef DIGITAL
    initial begin
        //$readmemh("/home/alexander/Documents/Organizacion de Computadoras/MIPS32SOC_Part1_Template/test_lb_data.mif", memory, 0, 1023);
	memory[0]=32'b0;
    end
`endif 
endmodule
*/

/* Code of DataMemVGA:
module DataMemVGA(
    input clk, //! Clock input
    input en, //! Enable
    input [3:0] we, //! Per byte write enable
    input [10:0] addr, //! Address
    input [31:0] wd, //! Write data
    output [31:0] rd //! Read data
);
 
    reg [31:0] memory[0:2047];
 
    assign rd = en? memory[addr] : 32'hz;
 
    always @(posedge clk)
    begin
        if (en) begin
            if (we[3]) memory[addr][7:0] <= wd[7:0];
            if (we[2]) memory[addr][15:8] <= wd[15:8];
            if (we[1]) memory[addr][23:16] <= wd[23:16];
            if (we[0]) memory[addr][31:24] <= wd[31:24];
        end
    end
 
`ifndef DIGITAL
    initial begin
        //$readmemh("data.mif", memory, 0, 1023);
    end
`endif 
endmodule
*/

/* Code of MemoryRDataDecoder:
module MemoryRDataDecoder(
    input [31:0] inD,
    input [1:0] ofs,
    input bitX,
    input [1:0] ds,
    output reg[31:0] oD
);

always @(*)
    case (ds)
      2'b00://Word
      begin
        oD=inD;
      end
      2'b01://Half-Word
      begin
        case (ofs)
          2'b00:
              begin
                if(bitX) begin//do signExtend
                  oD={ {16{inD[31]}},inD[31:16]};
                end else begin
                  oD={16'b0,inD[31:16]};
                end
              end
              2'b01:
              begin
                if(bitX) begin//do signExtend
                  oD={ {16{inD[31]}},inD[31:16]};
                end else begin
                  oD={16'b0,inD[31:16]};
                end
              end
              2'b10:
              begin
                if(bitX) begin
                oD={ {16{inD[15]}},inD[15:0]};
                end else begin
                oD={16'b0,inD[15:0]};
                end
              end
              2'b11:
              begin
                if(bitX) begin
                oD={ {16{inD[15]}},inD[15:0]};
                end else begin
                oD={16'b0,inD[15:0]};
                end
              end
        endcase
      end 
      2'b10://Byte
      begin
        case (ofs)
          2'b00:
              begin
                if(bitX) begin//do signExtend
                  oD={ {24{inD[31]}} ,inD[31:24]};
                end else begin
                  oD={24'b0,inD[31:24]};
                end
              end
              2'b01:
              begin
                if(bitX) begin//do signExtend
                  oD={ {24{inD[23]}},inD[23:16]};
                end else begin
                  oD={24'b0,inD[23:16]};
                end
              end
              2'b10:
              begin
                if(bitX) begin//do signExtend
                  oD={ {24{inD[15]}},inD[15:8]};
                end else begin
                  oD={24'b0,inD[15:8]};
                end
              end
              2'b11:
              begin
                if(bitX) begin//do signExtend
                  oD={ {24{inD[7]}},inD[7:0]};
                end else begin
                  oD={24'b0,inD[7:0]};
                end
              end
        endcase
      end
      default: 
        oD=31'b0;
    endcase
endmodule
*/
