// Digital circuit testPcDecoder.dig as structural Verilog
module testPcDecoder (
  input  [31:0] inp,
  output [9:0] ppc,
  output ipc
);

  pcdecoder #(.applicationType("IVERILOG")) u_pcdecoder (.vpc(inp), .ppc(ppc), .invpc(ipc));
  // Probe on ipc
endmodule

/* Test case:
		inp     ppc  ipc
repeat (4)  (0x400000+n) (n)    0
            0x401000      X     1
            0x3FFFFC      X     1
            0x400FFF      0xFFF 0
*/

/* Code of pcdecoder:
module pcdecoder(
    input [31:0] vpc,
    output reg[9:0] ppc,
    output reg invpc
);

parameter [31:0] startp=32'h400000 ;
parameter [31:0] endp=32'h401000 ;

always @(*)
begin
    if(vpc>=startp 
    & vpc<endp)begin
            ppc = vpc - startp;
	    invpc = 1'b0;
    end else begin
        invpc = 1'b1;
        ppc = 7'dx;
    end
end
endmodule
*/
