// Digital circuit MIPS32CPU.dig as structural Verilog
module MIPS32CPU (
  input  clk
);

  wire ALUsrc, and_1_out, and_2_out, branch, branche, isZ, jump, memread, memtoReg, memwrite, not_1_out,
       or_1_out, RegDst, regwrite;
  wire [1:0] ALUop;
  wire [2:0] opcontrol;
  wire [4:0] multiplexer_3_out;
  wire [5:0] func;
  wire [15:6] i_15_0;
  wire [31:0] multiplexer_1_out, multiplexer_2_out, multiplexer_4_out, pc_plus_4_s, PC_q, rwd, SignEx_out,
       u_alu_r, u_BranchTarget_out, u_datamemory_rdata, u_JumpTarget_out, u_regfile_da, u_regfile_db;
  wire [31:16] Ins;

  Register #(.Bits(32)) PC (.D(multiplexer_2_out), .C(clk), .en(1'b1), .Q(PC_q));
  Add #(.Bits(32)) pc_plus_4 (.a(PC_q), .b(32'h4), .c_i(1'b0), .s(pc_plus_4_s));  // open: c_o
  ROM #(.AddrBits(8), .Bits(32)) Ins_mem (.A(PC_q[9:2]), .sel(1'b1), .D({Ins, i_15_0, func}));
  JumpTarget #(.applicationType("IVERILOG")) u_JumpTarget (
    .in({Ins[25:16], i_15_0, func}), .pc4(pc_plus_4_s), .out(u_JumpTarget_out));
  BranchTarget #(.applicationType("IVERILOG")) u_BranchTarget (
    .imm({i_15_0, func}), .pc4(pc_plus_4_s), .out(u_BranchTarget_out));
  // Probe on {Ins, i_15_0, func}
  Multiplexer #(.Bits(32)) multiplexer_1 (
    .sel(or_1_out), .in_0(pc_plus_4_s), .in_1(u_BranchTarget_out), .out(multiplexer_1_out));
  or or_1 (or_1_out, and_1_out, and_2_out);
  and and_1 (and_1_out, isZ, branch);
  Multiplexer #(.Bits(32)) multiplexer_2 (
    .sel(jump), .in_0(multiplexer_1_out), .in_1(u_JumpTarget_out), .out(multiplexer_2_out));
  and and_2 (and_2_out, branche, not_1_out);
  not not_1 (not_1_out, isZ);
  Multiplexer #(.Bits(5)) multiplexer_3 (
    .sel(RegDst), .in_0(Ins[20:16]), .in_1(i_15_0[15:11]), .out(multiplexer_3_out));
  controlunit #(.applicationType("IVERILOG")) u_controlunit (
    .opcode(Ins[31:26]), .RegDst(RegDst), .branch(branch), .memread(memread), .memwrite(memwrite),
    .memtoReg(memtoReg), .ALUop(ALUop), .Alusrc(ALUsrc), .regwrite(regwrite), .jump(jump), .bne(branche));
  // Probe on rwd
  regfile #(.applicationType("IVERILOG")) u_regfile (
    .clk(clk), .Ra(Ins[25:21]), .Rb(Ins[20:16]), .Rw(multiplexer_3_out), .we(regwrite), .din(rwd),
    .Da(u_regfile_da), .Db(u_regfile_db));
  BitExtender #(.inputBits(16), .outputBits(32)) SignEx (.in({i_15_0, func}), .out(SignEx_out));
  Multiplexer #(.Bits(32)) multiplexer_4 (
    .sel(ALUsrc), .in_0(u_regfile_db), .in_1(SignEx_out), .out(multiplexer_4_out));
  // Probe on u_regfile_da
  alu #(.applicationType("IVERILOG")) u_alu (
    .a(u_regfile_da), .b(multiplexer_4_out), .op(opcontrol), .r(u_alu_r), .isZ(isZ));
  alucontrol #(.applicationType("IVERILOG")) u_alucontrol (.aluop(ALUop), .func(func), .op(opcontrol));
  Multiplexer #(.Bits(32)) multiplexer_5 (.sel(memtoReg), .in_0(u_alu_r), .in_1(u_datamemory_rdata), .out(rwd));
  datamemory #(.applicationType("IVERILOG")) u_datamemory (
    .clk(clk), .addr(u_alu_r[9:2]), .wData(u_regfile_db), .mwrite(memread), .mread(memwrite),
    .rdata(u_datamemory_rdata));

  // Other names for the same wires on the sheet: i_15_0[5:0] = func; Ins[15:0] = {i_15_0, func};
  //   sa[4:0] = i_15_0[10:6]; rd[4:0] = i_15_0[15:11]; rt[4:0] = Ins[20:16]; rs[4:0] = Ins[25:21];
  //   op[5:0] = Ins[31:26]

  // Notes on the sheet:
  //   clk: Hz: 5
  //   contents of Ins_mem (hex, n*v repeats v):
  //   a4302a,10c10005,433820,601020,e01820,a02820,8000000,601820,8000007
endmodule

/* Code of JumpTarget:
module JumpTarget(
	input [25:0] in,
	input [31:0] pc4,
	output [31:0] out 
);

assign out = {pc4[31:28], in, 2'b0};

endmodule
*/

/* Code of BranchTarget:
module BranchTarget(
	input [15:0] imm,
	input [31:0] pc4,
	output [31:0] out
);

wire [31:0] signExt;

assign signExt = {{16{imm[15]}}, imm};

assign out = {signExt[29:0], 2'b0} + pc4;

endmodule
*/

/* Code of controlunit:
module controlunit(
    input [5:0] opcode,
    output reg RegDst,
    output reg branch,
    output reg memread,
    output reg memwrite,
    output reg memtoReg,
    output reg [1:0]ALUop,
    output reg Alusrc,
    output reg regwrite,
    output reg jump,
    output reg bne
);

always @(*)
begin
    case (opcode)
      6'd0://R-Format((add,sub,and,or,slt)
            {RegDst,Alusrc,memtoReg,regwrite,memread,memwrite,branch,ALUop,jump,bne} = {1'b1,1'b0,1'b0,1'b1,1'b0,1'b0,1'b0,2'b10,1'b0,1'b0};
      6'd2://Jump
            {RegDst,Alusrc,memtoReg,regwrite,memread,memwrite,branch,ALUop,jump,bne} = {1'b0,1'b0,1'b0,1'b0,1'b0,1'b0,1'b0,2'b00,1'b1,1'b0};
      6'd4://beq
            {RegDst,Alusrc,memtoReg,regwrite,memread,memwrite,branch,ALUop,jump,bne} = {1'b0,1'b0,1'b0,1'b0,1'b0,1'b0,1'b1,2'b01,1'b0,1'b0};
      6'd5://bne
            {RegDst,Alusrc,memtoReg,regwrite,memread,memwrite,branch,ALUop,jump,bne} = {1'b0,1'b0,1'b0,1'b0,1'b0,1'b0,1'b0,2'b01,1'b0,1'b1};
      6'd35://load
            {RegDst,Alusrc,memtoReg,regwrite,memread,memwrite,branch,ALUop,jump,bne} = {1'b0,1'b1,1'b1,1'b1,1'b1,1'b0,1'b0,2'b00,1'b0,1'b0};
      6'd43://store
            {RegDst,Alusrc,memtoReg,regwrite,memread,memwrite,branch,ALUop,jump,bne} = {1'b0,1'b1,1'b0,1'b0,1'b0,1'b1,1'b0,2'b00,1'b0,1'b0};

      default: 
            {RegDst,Alusrc,memtoReg,regwrite,memread,memwrite,branch,ALUop,jump,bne} = {1'bx,1'bx,1'bx,1'bx,1'bx,1'bx,1'bx,2'bxx,1'bx,1'bx};
    endcase
end

endmodule
*/

/* Code of regfile:
module regfile(
input clk,
input [4:0]Ra,
input [4:0]Rb,
input [4:0]Rw,
input we,
input [31:0]din,
output reg [31:0]Da,
output reg [31:0]Db
);

reg [31:0] memory[31:0];

//seteando registros
initial begin
	    memory[0]=32'd0;
	    memory[1]=32'd1;
	    memory[2]=32'd0;
            memory[3]=32'd1;
	    memory[4]=32'd5;
	    memory[5]=32'd1;
	    
end

always @(posedge clk)
begin
    if(we)
        memory[Rw]<=din;
    

end

always @(*)
begin
  
    
    Da<=memory[Ra];
    Db<=memory[Rb];
end
endmodule
*/

/* Code of alu:
module alu(
	input[31:0] a,
	input[31:0] b,
	input[2:0] op,
	output reg[31:0] r,
	output isZ
);

assign isZ = r == 32'd0;

always@(*)
begin
	case(op)
		3'd0: r = a + b;
		3'd1: r = a - b;
		3'd2: r = a & b;
		3'd3: r = a | b;
		3'd4: r = {31'd0, $signed(a) < $signed(b)};
		default: r = 32'dX;
	endcase
end

endmodule
*/

/* Code of alucontrol:
module alucontrol(
    input [1:0] aluop,
    input [5:0] func,
    output reg[2:0] op
);


always @(*)
begin
    case (aluop)
      2'b00:
            op = 3'd0;//suma para lw y sw
      2'b01:
            op = 3'd1;//resta para el beq
      2'b10://R-Format
            case (func)
                6'b100000:
                        op = 3'd0;//suma 
                6'b100010:
                        op = 3'd1;//resta
                6'b100100:
                        op = 3'd2;//AND
                6'b100101:
                        op = 3'd3;//OR
                6'b101010:
                        op = 3'd4;//set less than
            default: 
                        op = 3'dx;
            endcase
      default:
            op = 3'dx; 
    endcase
end

endmodule
*/

/* Code of datamemory:
module datamemory(
    input clk,
    input [7:0]addr,
    input [31:0]wData,
    input mwrite,
    input mread,
    output reg[31:0]rdata
); 

reg [63:0] memory[31:0];

always @(posedge clk)
begin
    if(mwrite)
        memory[addr]<=wData;
end

always @(*)
begin
    if(mread)
    	rdata<=memory[addr];
end

endmodule
*/
