// Digital circuit MIPS32CPU.dig as structural Verilog
module MIPS32CPU (
  input  CLK,
  input  reset,
  output invpc,
  output iAddr,
  output [31:0] t_0,
  output [31:0] t_1,
  output [31:0] t_2,
  output [10:0] error,
  output iOp,
  output [31:0] w_0,
  output [31:0] t_3
);

  wire alurt, ALUsrc, bgez, bgtz, blez, bltz, branch, branche, branchtaken, btX, datamEn, immS, IOEn, isZ,
       jal, jr, jump, memread, memwrite, not_1_out, regwrite, u_cpustop_stop, VGAEn;
  wire [1:0] alurs, dS, mB, memtoReg, offs, RegDst;
  wire [2:0] ALUop;
  wire [3:0] opcontrol, u_MemoryWDataEncoder_owe;
  wire [4:0] multiplexer_6_out;
  wire [5:0] func;
  wire [7:0] UP_out;
  wire [9:0] u_pcdecoder_ppc, u_shift_out;
  wire [10:0] dmAddr, IOAddr, VGAAddr;
  wire [12:2] phyAddr;
  wire [15:6] i_15_0;
  wire [31:0] DMrd, iord, mscounter_1_p2, multiplexer_1_out, multiplexer_2_out, multiplexer_3_out,
       multiplexer_4_out, multiplexer_7_out, multiplexer_8_out, multiplexer_9_out, multiplexer_10_out,
       multiplexer_12_out, next_pc, pc_plus_4, PC_q, regA, rvAddr, rwd, SignEx_2_out, SignEx_out,
       u_BranchTarget_out, u_JumpTarget_out, u_lui_res, u_MemoryRDataDecoder_od, u_MemoryWDataEncoder_od,
       u_regfile_db, u_zeroExtension_res, VGArd;
  wire [31:16] Ins;

  cpustop #(.applicationType("IVERILOG")) u_cpustop (.ipc(invpc), .iAd(iAddr), .iOp(iOp), .stop(u_cpustop_stop));
  Multiplexer #(.Bits(32)) multiplexer_1 (
    .sel(reset), .in_0(32'h400000), .in_1(multiplexer_2_out), .out(multiplexer_1_out));
  Multiplexer #(.Bits(32)) multiplexer_2 (
    .sel(u_cpustop_stop), .in_0(next_pc), .in_1({32{1'b0}}), .out(multiplexer_2_out));
  Register #(.Bits(32)) PC (.D(multiplexer_1_out), .C(CLK), .en(1'b1), .Q(PC_q));
  pcdecoder #(.applicationType("IVERILOG")) u_pcdecoder (.vpc(PC_q), .ppc(u_pcdecoder_ppc), .invpc(invpc));
  Add #(.Bits(32)) u_pc_plus_4 (.a(PC_q), .b(32'h4), .c_i(1'b0), .s(pc_plus_4));  // open: c_o
  // Probe on {Ins[25:16], i_15_0, func}
  JumpTarget #(.applicationType("IVERILOG")) u_JumpTarget (
    .in({Ins[25:16], i_15_0, func}), .pc4(pc_plus_4), .out(u_JumpTarget_out));
  BranchTarget #(.applicationType("IVERILOG")) u_BranchTarget (
    .imm({i_15_0, func}), .pc4(pc_plus_4), .out(u_BranchTarget_out));
  shift #(.applicationType("IVERILOG")) u_shift (.in(u_pcdecoder_ppc), .out(u_shift_out));
  ROM #(.AddrBits(10), .Bits(32)) Ins_mem (.A(u_shift_out), .sel(1'b1), .D({Ins, i_15_0, func}));
  Multiplexer #(.Bits(32)) multiplexer_3 (
    .sel(branchtaken), .in_0(pc_plus_4), .in_1(u_BranchTarget_out), .out(multiplexer_3_out));
  // Probe on pc_plus_4
  // Probe on u_JumpTarget_out
  Multiplexer #(.Bits(32)) multiplexer_4 (
    .sel(jump), .in_0(multiplexer_3_out), .in_1(u_JumpTarget_out), .out(multiplexer_4_out));
  controlunit #(.applicationType("IVERILOG")) u_controlunit (
    .opcode(Ins[31:26]), .func(func), .rt(Ins[20:16]), .RegDst(RegDst), .branch(branch), .memread(memread),
    .memwrite(memwrite), .memtoReg(memtoReg), .ALUop(ALUop), .Alusrc(ALUsrc), .regwrite(regwrite),
    .jump(jump), .bne(branche), .immS(immS), .dS(dS), .btX(btX), .iOp(iOp), .bgez(bgez), .bgtz(bgtz),
    .blez(blez), .bltz(bltz), .jal(jal), .jr(jr));
  Multiplexer #(.Bits(32)) multiplexer_5 (.sel(jr), .in_0(multiplexer_4_out), .in_1(regA), .out(next_pc));
  alucontrol #(.applicationType("IVERILOG")) u_alucontrol (
    .aluop(ALUop), .func(func), .op(opcontrol), .alurt(alurt), .alurssa(alurs));
  Multiplexer #(.Selector_Bits(2), .Bits(5)) multiplexer_6 (
    .sel(RegDst), .in_0(Ins[20:16]), .in_1(i_15_0[15:11]), .in_2({5{1'b1}}), .in_3({5{1'b0}}),
    .out(multiplexer_6_out));
  BitExtender #(.inputBits(16), .outputBits(32)) SignEx (.in({i_15_0, func}), .out(SignEx_out));
  zeroExtension #(.applicationType("IVERILOG")) u_zeroExtension (.n({i_15_0, func}), .res(u_zeroExtension_res));
  // Probe on rwd
  regfile #(.applicationType("IVERILOG")) u_regfile (
    .clk(CLK), .Ra(Ins[25:21]), .Rb(Ins[20:16]), .Rw(multiplexer_6_out), .we(regwrite), .din(rwd), .Da(regA),
    .Db(u_regfile_db), .t_0(t_0), .t_1(t_1), .t_2(t_2), .t_3(t_3));
  BitExtender #(.inputBits(5), .outputBits(32)) SignEx_2 (.in(i_15_0[10:6]), .out(SignEx_2_out));
  Multiplexer #(.Bits(32)) multiplexer_7 (
    .sel(immS), .in_0(SignEx_out), .in_1(u_zeroExtension_res), .out(multiplexer_7_out));
  branchresolver #(.applicationType("IVERILOG")) u_branchresolver (
    .beq(branch), .bne(branche), .bgez(bgez), .bgtz(bgtz), .blez(blez), .bltz(bltz), .zero(isZ),
    .sign(regA[31]), .bt(branchtaken));
  Multiplexer #(.Bits(32)) multiplexer_8 (.sel(alurt), .in_0(regA), .in_1(u_regfile_db), .out(multiplexer_8_out));
  Multiplexer #(.Bits(32)) multiplexer_9 (
    .sel(ALUsrc), .in_0(u_regfile_db), .in_1(multiplexer_7_out), .out(multiplexer_9_out));
  Demultiplexer #(.Selector_Bits(2), .Bits(11)) demultiplexer_1 (
    .sel(mB), .in(phyAddr), .out_0(dmAddr), .out_1(VGAAddr), .out_2(IOAddr), .out_3(error));
  Multiplexer #(.Selector_Bits(2), .Bits(32)) multiplexer_10 (
    .sel(alurs), .in_0(multiplexer_9_out), .in_1(SignEx_2_out), .in_2(regA), .in_3({32{1'b0}}),
    .out(multiplexer_10_out));
  lui #(.applicationType("IVERILOG")) u_lui (.n({i_15_0, func}), .res(u_lui_res));
  memoryDecoder #(.applicationType("IVERILOG")) u_memoryDecoder (
    .vAddr(rvAddr), .mW(memwrite), .mR(memread), .pAd({phyAddr, offs}), .mE({IOEn, VGAEn, datamEn}), .mB(mB),
    .iAd(iAddr));
  MemoryWDataEncoder #(.applicationType("IVERILOG")) u_MemoryWDataEncoder (
    .inD(u_regfile_db), .ofs(offs), .iwe(memwrite), .ds(dS), .oD(u_MemoryWDataEncoder_od),
    .owe(u_MemoryWDataEncoder_owe));
  alu #(.applicationType("IVERILOG")) u_alu (
    .a(multiplexer_8_out), .b(multiplexer_10_out), .op(opcontrol), .r(rvAddr), .isZ(isZ));
  // Probe on rvAddr
  Multiplexer #(.Selector_Bits(2), .Bits(32)) multiplexer_11 (
    .sel(memtoReg), .in_0(rvAddr), .in_1(u_MemoryRDataDecoder_od), .in_2(u_lui_res), .in_3(pc_plus_4),
    .out(rwd));
  Button RIGHT (.out(UP_out[1]));
  Button DOWN (.out(UP_out[2]));
  Button UP (.out(UP_out[3]));
  Button Q (.out(UP_out[4]));
  Button P (.out(UP_out[5]));
  Button B (.out(UP_out[6]));
  // Probe on memtoReg
  Button LEFT (.out(UP_out[0]));
  Button S (.out(UP_out[7]));
  DataMem #(.applicationType("IVERILOG")) u_DataMem (
    .clk(CLK), .en(datamEn), .we(u_MemoryWDataEncoder_owe), .addr(dmAddr), .wd(u_MemoryWDataEncoder_od),
    .rd(DMrd), .w(w_0));
  // MsCounter mscounter_1: pin names not known; wires that end beside it: CLK, mscounter_1_p2
  VGA80X30Sim u_VGA80X30Sim (
    .vclk(CLK), .clk(CLK), .rst(not_1_out), .en(VGAEn), .we(u_MemoryWDataEncoder_owe), .addr(VGAAddr),
    .wd(u_MemoryWDataEncoder_od), .rd(VGArd));
  not not_1 (not_1_out, reset);
  iomemory #(.applicationType("IVERILOG")) u_iomemory (
    .en(IOEn), .addr(IOAddr), .keypad(UP_out), .mscounter(mscounter_1_p2), .rd(iord));
  Multiplexer #(.Selector_Bits(2), .Bits(32)) multiplexer_12 (
    .sel(mB), .in_0(DMrd), .in_1(VGArd), .in_2(iord), .in_3({32{1'b0}}), .out(multiplexer_12_out));
  MemoryRDataDecoder #(.applicationType("IVERILOG")) u_MemoryRDataDecoder (
    .inD(multiplexer_12_out), .ofs(offs), .bitX(btX), .ds(dS), .oD(u_MemoryRDataDecoder_od));

  // Other names for the same wires on the sheet: i_15_0[5:0] = func; Ins[15:0] = {i_15_0, func};
  //   sa[4:0] = i_15_0[10:6]; rd[4:0] = i_15_0[15:11]; rt[4:0] = Ins[20:16]; rs[4:0] = Ins[25:21];
  //   op[5:0] = Ins[31:26]; phyAddr[1:0] = offs; rst = reset

  // Notes on the sheet:
  //   CLK: Hz: 5
  //   contents of Ins_mem (hex, n*v repeats v):
  //   3c1d7fff,37bdfffc,c100021,8100003,41080,442021,42140,3c020001,822021,2402cf00,a22825,
  //   a485b802,3e00008,41080,442021,42100,852021,42040,3405b800,a42021,2403cf00,3405cac0,
  //   80c20000,14400001,3e00008,431025,85382b,3042ffff,24c60001,10e0fffa,24840002,a482fffe,
  //   1000fff5,27bdffd8,3402b800,24043020,afbf0024,afb10020,afb0001c,3403cac0,a4440000,
  //   24420002,1443fffd,3402b800,2403c20a,3404b8a0,a4430000,a4431220,24420002,1444fffc,
  //   3402b800,2403c20a,3404ca20,a4430000,a443009e,244200a0,1444fffc,3c0b1001,25660000,
  //   2405001e,2404000f,c10000d,3c02ffff,3c0f1001,8c590008,7025,afa00010,afa00014,2409001e,
  //   2408000f,25ef0014,256b0000,2410004e,3c03ffff,906d0004,8c620008,31ad00ff,591023,2c4203e9,
  //   14400002,8c790008,25ce0001,31c2000f,304300ff,2c42000a,24650057,10400001,24650030,
  //   24040001,c100004,31a2000f,2c43000a,24450057,10600001,24450030,24040002,c100004,27ac0010,
  //   5025,24180001,14d1006,30420001,91830000,305100ff,10710010,1040000e,1e03025,1202825,
  //   1002025,c10000d,11580016,1140000e,24020002,1142001b,24020003,1142001d,1603025,1202825,
  //   1002025,c10000d,a1910000,254a0001,24020008,258c0001,1542ffe7,1000ffcb,15380004,11090014,
  //   2508ffff,2409004e,1000fff1,2529ffff,1000ffef,15300005,24020026,1102000f,25080001,
  //   24090001,1000ffe9,25290001,1000ffe7,2402001c,11020009,25080001,1000ffe3,11180003,
  //   2508ffff,1000ffe0,2409004e,2408001c,1000ffdd,24090001,24080001,1000ffda
endmodule

/* Code of cpustop:
module cpustop(
    input ipc,
    input iAd,
    input iOp,
    output reg stop
);

always @(*)
if(ipc | iAd | iOp) begin
  stop = 1'b1;
end else begin
  stop = 1'b0;
end

endmodule
*/

/* Code of pcdecoder:
module pcdecoder(
    input [31:0] vpc,
    output reg[9:0] ppc,
    output reg invpc
);

parameter [31:0] startp=32'h400000 ;
parameter [31:0] endp=32'h401000 ;

always @(*)
begin
    if(vpc>=startp 
    & vpc<endp)begin
            ppc = vpc - startp;
	    invpc = 1'b0;
    end else begin
        invpc = 1'b1;
        ppc = 7'dx;
    end
end
endmodule
*/

/* Test case:
CLK reset t_0         t_1     t_2 t_3
C   0   x           x       x   x
C   1   4           x       x   x
C   1   4           x       x   x
C   1   0xaabb0000  x       x   x
C   1   0xaabbccdd  x       x   x
C   1   0xaabbccdd  x       x   x
C   1   0xaabbccdd  x       x   x
C   1   0xaa        x       x   x
C   1   0xaa        x       x   x
*/

/* Code of JumpTarget:
module JumpTarget(
	input [25:0] in,
	input [31:0] pc4,
	output [31:0] out 
);

assign out = {pc4[31:28], in, 2'b0};

endmodule
*/

/* Code of BranchTarget:
module BranchTarget(
	input [15:0] imm,
	input [31:0] pc4,
	output [31:0] out
);

wire [31:0] signExt;

assign signExt = {{16{imm[15]}}, imm};

assign out = {signExt[29:0], 2'b0} + pc4;

endmodule
*/

/* Code of shift:
module shift(
	input [9:0] in,
	output [9:0] out
);

assign out = in >> 2;

endmodule
*/

/* Code of controlunit:
module controlunit(
    input [5:0] opcode,
    input [5:0] func,
    input [4:0] rt,
    output reg [1:0]RegDst,
    output reg branch,
    output reg memread,
    output reg memwrite,
    output reg [1:0]memtoReg,
    output reg [2:0]ALUop,
    output reg Alusrc,
    output reg regwrite,
    output reg jump,
    output reg bne,
    output reg immS,
    output reg [1:0]dS,
    output reg btX,
    output reg iOp,
    output reg bgez,
    output reg bgtz,
    output reg blez,
    output reg bltz,
    output reg jal,
    output reg jr
);

always @(*)
begin
    case (opcode)
      6'd0://R-Format((add,sub,and,or,slt)//entrega4(sll,srl,sra,sllv,srlv,srav,)
      begin
            if(func==6'd8) begin
            {RegDst,Alusrc,memtoReg,regwrite,memread,memwrite,branch,ALUop, jump, bne, immS} = 
            {2'b01, 1'b0,  2'b00,   1'b0,    1'b0,   1'b0,    1'b0,  3'b000,1'b0, 1'b0,1'b0};
            dS=2'b00;
            btX=1'b0;
            iOp = 1'b0;
            bgez = 1'b0;
            bgtz = 1'b0;
            blez = 1'b0;
            bltz = 1'b0;
            jal = 1'b0;
            jr = 1'b1;
            end else begin
            {RegDst,Alusrc,memtoReg,regwrite,memread,memwrite,branch,ALUop, jump, bne, immS} = 
            {2'b01, 1'b0,  2'b00,   1'b1,    1'b0,   1'b0,    1'b0,  3'b010,1'b0, 1'b0,1'b0};
            dS=2'b00;
            btX=1'b0;
            iOp = 1'b0;
            bgez = 1'b0;
            bgtz = 1'b0;
            blez = 1'b0;
            bltz = 1'b0;
            jal = 1'b0;
            jr = 1'b0;
            end
      end
      6'd1://BGEZ o BLTZ
      begin
            if(rt==5'd1)begin//BGEZ
            {RegDst,Alusrc,memtoReg,regwrite,memread,memwrite,branch,ALUop, jump,bne, immS} =
            {2'b00, 1'b0,  2'b00,   1'b0,    1'b0,   1'b0,    1'b0,  3'b000,1'b0,1'b0,1'b0};
            dS=2'b00;
            btX=1'b0;
            iOp = 1'b0;
            bgez = 1'b1;
            bgtz = 1'b0;
            blez = 1'b0;
            bltz = 1'b0;
            jr = 1'b0;
            jal = 1'b0;
            end else begin//BLTZ
            {RegDst,Alusrc,memtoReg,regwrite,memread,memwrite,branch,ALUop, jump,bne, immS} =
            {2'b00, 1'b0,  2'b00,   1'b0,    1'b0,   1'b0,    1'b0,  3'b000,1'b0,1'b0,1'b0};
            dS=2'b00;
            btX=1'b0;
            iOp = 1'b0;
            bgez = 1'b0;
            bgtz = 1'b0;
            blez = 1'b0;
            bltz = 1'b1;
            jr = 1'b0;
            jal = 1'b0;
            end
      end
      6'd2://Jump
      begin
            {RegDst,Alusrc,memtoReg,regwrite,memread,memwrite,branch,ALUop,jump,bne,immS} = {2'b00,1'b0,2'b00,1'b0,1'b0,1'b0,1'b0,3'b000,1'b1,1'b0,1'b0};
            dS=2'b00;
            btX=1'b0;
            iOp = 1'b0;
            bgez = 1'b0;
            bgtz = 1'b0;
            blez = 1'b0;
            bltz = 1'b0;
            jr = 1'b0;
            jal = 1'b0;
           
      end
      6'd3://JAL
      begin
            {RegDst,Alusrc,memtoReg,regwrite,memread,memwrite,branch,ALUop,jump,bne,immS} = 
            {2'b10, 1'b0,  2'b11,   1'b1,    1'b0,   1'b0,    1'b0,  3'b000,1'b1,1'b0,1'b0};
            dS=2'b00;
            btX=1'b0;
            iOp = 1'b0;
            bgez = 1'b0;
            bgtz = 1'b0;
            blez = 1'b0;
            bltz = 1'b0;
            jal = 1'b1;
            jr = 1'b0;
           
      end
       
      6'd4://beq
      begin
            {RegDst,Alusrc,memtoReg,regwrite,memread,memwrite,branch,ALUop,jump,bne,immS} =
             {2'b00,1'b0,2'b00,1'b0,1'b0,1'b0,1'b1,3'b001,1'b0,1'b0,1'b0};
            dS=2'b00;
            btX=1'b0;
            iOp = 1'b0;
            bgez = 1'b0;
            bgtz = 1'b0;
            blez = 1'b0;
            bltz = 1'b0;
            jr = 1'b0;
            jal = 1'b0;
            
      end
      6'd5://bne
      begin
            {RegDst,Alusrc,memtoReg,regwrite,memread,memwrite,branch,ALUop,jump,bne,immS} = {2'b00,1'b0,2'b00,1'b0,1'b0,1'b0,1'b0,3'b001,1'b0,1'b1,1'b0};
            dS=2'b00;
            btX=1'b0;
            iOp = 1'b0;
            bgez = 1'b0;
            bgtz = 1'b0;
            blez = 1'b0;
            bltz = 1'b0;
            jr = 1'b0;
            jal = 1'b0;
         
      end
      6'd6://blez
      begin
      {RegDst,Alusrc,memtoReg,regwrite,memread,memwrite,branch,ALUop, jump,bne, immS} =
            {2'b00, 1'b0,  2'b00,   1'b0,    1'b0,   1'b0,    1'b0,  3'b000,1'b0,1'b0,1'b0};
            dS=2'b00;
            btX=1'b0;
            iOp = 1'b0;
            bgez = 1'b0;
            bgtz = 1'b0;
            blez = 1'b1;
            bltz = 1'b0;
            jr = 1'b0;
            jal = 1'b0;
      end
      6'd7://bgtz
      begin
      {RegDst,Alusrc,memtoReg,regwrite,memread,memwrite,branch,ALUop, jump,bne, immS} =
            {2'b00, 1'b0,  2'b00,   1'b0,    1'b0,   1'b0,    1'b0,  3'b000,1'b0,1'b0,1'b0};
            dS=2'b00;
            btX=1'b0;
            iOp = 1'b0;
            bgez = 1'b0;
            bgtz = 1'b1;
            blez = 1'b0;
            bltz = 1'b0;
            jr = 1'b0;
            jal = 1'b0;
      end
      6'd8://addi
      begin
            {RegDst,Alusrc,memtoReg,regwrite,memread,memwrite,branch,ALUop,jump,bne,immS} = {2'b00,1'b1,2'b00,1'b1,1'b0,1'b0,1'b0,3'b000,1'b0,1'b0,1'b0};
            dS=2'b00;
            btX=1'b0;
            iOp = 1'b0;
            bgez = 1'b0;
            bgtz = 1'b0;
            blez = 1'b0;
            bltz = 1'b0;
            jr = 1'b0;
            jal = 1'b0;
        
      end
      6'd9://addiu
      begin
            {RegDst,Alusrc,memtoReg,regwrite,memread,memwrite,branch,ALUop,jump,bne,immS} = {2'b00,1'b1,2'b00,1'b1,1'b0,1'b0,1'b0,3'b000,1'b0,1'b0,1'b0};
            dS=2'b00;
            btX=1'b0;
            iOp = 1'b0;
            bgez = 1'b0;
            bgtz = 1'b0;
            blez = 1'b0;
            bltz = 1'b0;
            jr = 1'b0;
            jal = 1'b0;
   
      end
      6'd10://slti
      begin
            {RegDst,Alusrc,memtoReg,regwrite,memread,memwrite,branch,ALUop,jump,bne,immS} = 
            {2'b00,  1'b1,  2'b00,   1'b1,    1'b0,   1'b0,    1'b0,  3'b110,1'b0,1'b0,1'b1};
            dS=2'b00;
            btX=1'b0;
            iOp = 1'b0;
            bgez = 1'b0;
            bgtz = 1'b0;
            blez = 1'b0;
            bltz = 1'b0;
            jr = 1'b0;
            jal = 1'b0;
  
      end
       6'd11://sltiu
      begin
            {RegDst,Alusrc,memtoReg,regwrite,memread,memwrite,branch,ALUop,jump,bne,immS} = 
            {2'b00,  1'b1,  2'b00,   1'b1,    1'b0,   1'b0,    1'b0,  3'b111,1'b0,1'b0,1'b0};
            dS=2'b00;
            btX=1'b0;
            iOp = 1'b0;
            bgez = 1'b0;
            bgtz = 1'b0;
            blez = 1'b0;
            bltz = 1'b0;
            jr = 1'b0;
            jal = 1'b0;
  
      end
      6'd12://andi
      begin
            {RegDst,Alusrc,memtoReg,regwrite,memread,memwrite,branch,ALUop,jump,bne,immS} = {2'b00,1'b1,2'b00,1'b1,1'b0,1'b0,1'b0,3'b011,1'b0,1'b0,1'b1};
            dS=2'b00;
            btX=1'b0;
            iOp = 1'b0;
            bgez = 1'b0;
            bgtz = 1'b0;
            blez = 1'b0;
            bltz = 1'b0;
            jr = 1'b0;
            jal = 1'b0;

      end
      6'd13://ori
      begin
            {RegDst,Alusrc,memtoReg,regwrite,memread,memwrite,branch,ALUop,jump,bne,immS} = {2'b00,1'b1,2'b00,1'b1,1'b0,1'b0,1'b0,3'b100,1'b0,1'b0,1'b1};
            dS=2'b00;
            btX=1'b0;
            iOp = 1'b0;
            bgez = 1'b0;
            bgtz = 1'b0;
            blez = 1'b0;
            bltz = 1'b0;
            jr = 1'b0;
            jal = 1'b0;
  
      end
      6'd14://xori
      begin
            {RegDst,Alusrc,memtoReg,regwrite,memread,memwrite,branch,ALUop,jump,bne,immS} = 
            {2'b00,  1'b1,  2'b00,   1'b1,    1'b0,   1'b0,    1'b0,  3'b101,1'b0,1'b0,1'b1};
            dS=2'b00;
            btX=1'b0;
            iOp = 1'b0;
            bgez = 1'b0;
            bgtz = 1'b0;
            blez = 1'b0;
            bltz = 1'b0;
            jr = 1'b0;
            jal = 1'b0;
  
      end
      6'd15://lui
      begin
            {RegDst,Alusrc,memtoReg,regwrite,memread,memwrite,branch,ALUop,jump,bne,immS} = {2'b00,1'b0,2'b10,1'b1,1'b0,1'b0,1'b0,3'b000,1'b0,1'b0,1'b0};
            dS=2'b00;
            btX=1'b0;
            iOp = 1'b0;
            bgez = 1'b0;
            bgtz = 1'b0;
            blez = 1'b0;
            bltz = 1'b0;
            jr = 1'b0;
            jal = 1'b0;
         
      end
      6'd32://lb
      begin
            {RegDst,Alusrc,memtoReg,regwrite,memread,memwrite,branch,ALUop,jump,bne,immS} 
          = {2'b00,   1'b1,  2'b01,   1'b1,    1'b1,   1'b0,    1'b0,3'b000, 1'b0,1'b0,1'b0};
            dS=2'b10;//0-Word,1-HWord,2-byte
            btX=1'b1;//1-SignEx,2-ZeroEx
            iOp = 1'b0;
            bgez = 1'b0;
            bgtz = 1'b0;
            blez = 1'b0;
            bltz = 1'b0;
            jr = 1'b0;
            jal = 1'b0;
  
      end
      6'd33://lh
      begin
            {RegDst,Alusrc,memtoReg,regwrite,memread,memwrite,branch,ALUop,jump,bne,immS} 
          = {2'b00,   1'b1,  2'b01,   1'b1,    1'b1,   1'b0,    1'b0,3'b000, 1'b0,1'b0,1'b0};
            dS=2'b01;//0-Word,1-HWord,2-byte
            btX=1'b1;//1-SignEx,2-ZeroEx
            iOp = 1'b0;
            bgez = 1'b0;
            bgtz = 1'b0;
            blez = 1'b0;
            bltz = 1'b0;
            jr = 1'b0;
            jal = 1'b0;
 
      end
      6'd35://loadword
      begin
            {RegDst,Alusrc,memtoReg,regwrite,memread,memwrite,branch,ALUop,jump,bne,immS} 
          = {2'b00,  1'b1,  2'b01,   1'b1,    1'b1,   1'b0,    1'b0,  3'b000,1'b0,1'b0,1'b0};
            dS=2'b00;//0-Word,1-HWord,2-byte
            btX=1'b1;//1-SignEx,2-ZeroEx
            iOp = 1'b0;
            bgez = 1'b0;
            bgtz = 1'b0;
            blez = 1'b0;
            bltz = 1'b0;
            jr = 1'b0;
            jal = 1'b0;

      end

      6'd36://lbu
      begin
            {RegDst,Alusrc,memtoReg,regwrite,memread,memwrite,branch,ALUop,jump,bne,immS} 
          = {2'b00,   1'b1,  2'b01,   1'b1,    1'b1,   1'b0,    1'b0,3'b000, 1'b0,1'b0,1'b0};
            dS=2'b10;//0-Word,1-HWord,2-byte
            btX=1'b0;//1-SignEx,2-ZeroEx
            iOp = 1'b0;
            bgez = 1'b0;
            bgtz = 1'b0;
            blez = 1'b0;
            bltz = 1'b0;
            jr = 1'b0;
            jal = 1'b0;
           
      end
      6'd37://lhu
      begin
            {RegDst,Alusrc,memtoReg,regwrite,memread,memwrite,branch,ALUop,jump,bne,immS} 
          = {2'b00,   1'b1,  2'b01,   1'b1,    1'b1,   1'b0,    1'b0,3'b000, 1'b0,1'b0,1'b0};
            dS=2'b01;//0-Word,1-HWord,2-byte
            btX=1'b0;//1-SignEx,2-ZeroEx1
            iOp = 1'b0;
            bgez = 1'b0;
            bgtz = 1'b0;
            blez = 1'b0;
            bltz = 1'b0;
            jr = 1'b0;
            jal = 1'b0;
      
      end
     6'd40://sb
      begin
            {RegDst,Alusrc,memtoReg,regwrite,memread,memwrite,branch,ALUop,jump,bne,immS} 
          = {2'b00,   1'b1,  2'b00,   1'b0,    1'b0,   1'b1,    1'b0,3'b000, 1'b0,1'b0,1'b0};
            dS=2'b10;//0-Word,1-HWord,2-byte
            btX=1'b0;//1-SignEx,2-ZeroEx
            iOp = 1'b0;
            bgez = 1'b0;
            bgtz = 1'b0;
            blez = 1'b0;
            bltz = 1'b0;
            jr = 1'b0;
            jal = 1'b0;
      end
      6'd41://sh
      begin
            {RegDst,Alusrc,memtoReg,regwrite,memread,memwrite,branch,ALUop,jump,bne,immS} 
          = {2'b00,   1'b1,  2'b00,   1'b0,    1'b0,   1'b1,    1'b0,3'b000, 1'b0,1'b0,1'b0};
            dS=2'b01;//0-Word,1-HWord,2-byte
            btX=1'b0;//1-SignEx,2-ZeroEx
            iOp = 1'b0;
            bgez = 1'b0;
            bgtz = 1'b0;
            blez = 1'b0;
            bltz = 1'b0;
            jr = 1'b0;
            jal = 1'b0;
            
      end
      6'd43://storeword
      begin
            {RegDst,Alusrc,memtoReg,regwrite,memread,memwrite,branch,ALUop,jump,bne,immS}
          = {2'b00,  1'b1,  2'b00,   1'b0,    1'b0,   1'b1,    1'b0,  3'b000,1'b0,1'b0,1'b0};
            dS=2'b00;//0-Word,1-HWord,2-byte
            btX=1'b0;//1-SignEx,2-ZeroEx
            iOp = 1'b0;
            bgez = 1'b0;
            bgtz = 1'b0;
            blez = 1'b0;
            bltz = 1'b0;
            jr = 1'b0;
            jal = 1'b0;
           
      end
      default: 
      begin
        {RegDst,Alusrc,memtoReg,regwrite,memread,memwrite,branch,ALUop,jump,bne} = {2'bxx,1'bx,2'bxx,1'bx,1'bx,1'bx,1'bx,3'bxxx,1'bx,1'bx,1'bx};
        dS=2'b00;
        btX=1'b0;
        iOp = 1'b1;
        bgez = 1'b0;
        bgtz = 1'b0;
        blez = 1'b0;
        bltz = 1'b0;
        jr = 1'b0;
        jal = 1'b0;
        
      end
            
    endcase
end

endmodule
*/

/* Code of alucontrol:
module alucontrol(
    input [2:0] aluop,
    input [5:0] func,
    output reg[3:0] op,
    output reg alurt,
    output reg [1:0] alurssa
);


always @(*)
begin
    case (aluop)
      3'b000:
      begin
            op = 4'd0;//suma para lw y sw
            alurt = 1'b0;
            alurssa = 2'd0;
      end
      3'b001:
      begin
            op = 4'd1;//resta para el beq
            alurt = 1'b0;
            alurssa = 2'd0;
      end
      3'b010://R-Format
            case (func)
                6'b000000://SLL
                begin
                        op = 4'd5;//shift left logic 
                        alurt = 1'b1;
                        alurssa = 2'd1;
                end
                6'b000010://SRL
                begin
                        op = 4'd6;//shift right logic 
                        alurt = 1'b1;
                        alurssa = 2'd1;
                end
                6'b000011://SRA
                begin
                        op = 4'd7;//shift right arithmetic
                        alurt = 1'b1;
                        alurssa = 2'd1;
                end
                6'b000100://SLLV
                begin
                        op = 4'd5;//shift left logic
                        alurt = 1'b1;
                        alurssa = 2'd2;//emtra rs como segundo
                end
                6'b000110://SRLV
                begin
                        op = 4'd6;//shift right logic
                        alurt = 1'b1;
                        alurssa = 2'd2;//emtra rs como segundo
                end
                6'b000111://SRAV
                begin
                        op = 4'd7;//shift right arithmetic
                        alurt = 1'b1;
                        alurssa = 2'd2;//emtra rs como segundo
                end
                6'b100000:
                begin
                        op = 4'd0;//suma 
                        alurt = 1'b0;
                        alurssa = 2'd0;
                end
                6'b100001:
                begin
                        op = 4'd0;//addu
                        alurt = 1'b0;
                        alurssa = 2'd0;
                end
                6'b100010:
                begin
                        op = 4'd1;//resta
                        alurt = 1'b0;
                        alurssa = 2'd0;
                end
                6'b100011:
                begin
                        op= 4'd1;//subu
                        alurt = 1'b0;
                        alurssa = 2'd0;
                end
                6'b100100:
                begin
                        op = 4'd2;//AND
                        alurt = 1'b0;
                        alurssa = 2'd0;
                end
                6'b100101:
                begin
                        op = 4'd3;//OR
                        alurt = 1'b0;
                        alurssa = 2'd0;
                end
                6'b100110://XOR
                begin
                        op = 4'd8;
                        alurt = 1'b0;
                        alurssa = 2'd0;
                end
                6'b101010:
                begin
                        op = 4'd4;//set less than
                        alurt = 1'b0;
                        alurssa = 2'd0;
                end
                6'b101011://SLTU
                begin
                        op = 4'd9;
                        alurt = 1'b0;
                        alurssa = 2'd0;
                end
            default: 
            begin
                        op = 4'dx;
                        alurt = 1'b0;
                        alurssa = 2'd0;
            end
            endcase
        
        3'b011://and
        begin
                op = 4'd2;
                alurt = 1'b0;
                alurssa = 2'd0;
        end
        3'b100://or
        begin
                op = 4'd3;
                alurt = 1'b0;
                alurssa = 2'd0;
        end
        3'b101://xor
        begin
                op = 4'd3;
                alurt = 1'b0;
                alurssa = 2'd0;
        end
        3'b110://lessthansigned
        begin
                op = 4'd4;
                alurt = 1'b0;
                alurssa = 2'd0;
        end
        3'b111://lessthanunsigned
        begin
                op = 4'd9;
                alurt = 1'b0;
                alurssa = 2'd0;
        end
      default:
      begin
            op = 4'dx;
            alurt = 1'b0;
            alurssa = 2'd0; 
      end
    endcase
end

endmodule
*/

/* Code of zeroExtension:
module zeroExtension(
    input [15:0] n,
    output [31:0] res
);

assign res = {16'b0,n};

endmodule
*/

/* Code of regfile:
module regfile(
input clk,
input [4:0]Ra,
input [4:0]Rb,
input [4:0]Rw,
input we,
input [31:0]din,
output reg [31:0]Da,
output reg [31:0]Db,
output [31:0] t_0,
output [31:0] t_1,
output [31:0] t_2,
output [31:0] t_3

);

reg [31:0] memory[31:0];
assign t_0 = memory[8];
assign t_1 = memory[9];
assign t_2 = memory[10];
assign t_3 = memory[11];

//seteando registros
//initial $readmemh("/home/alexander/Documents/MIPS32SOC-Part2/tests/hex/RegFile.mif", memory);
initial begin
memory[0] = 32'b0;
end

always @(posedge clk)
begin
    if(we & Rw > 0)
        memory[Rw]<=din;
    

end

always @(*)
begin
  
    
    Da<=memory[Ra];
    Db<=memory[Rb];
end
endmodule
*/

/* Code of branchresolver:
module branchresolver(
    input beq,
    input bne,
    input bgez,
    input bgtz,
    input blez,
    input bltz,
    input zero,
    input sign,
    output reg bt
);

always @(*)
begin
    if(beq & zero==1'b1)
        bt=1'b1;
    else if(bne & zero== 1'b0)
        bt=1'b1;
    else if(bgez & sign==1'b0)
        bt=1'b1;
    else if(bgtz & sign==1'b0 & zero==1'b0)
        bt=1'b1;
    else if(blez & (sign==1'b1 | zero==1'b1))
        bt=1'b1;
    else if(bltz & sign==1'b1)
        bt=1'b1;
    else
        bt=1'b0;
    
end

endmodule
*/

/* Code of lui:
module lui(
    input [15:0] n,
    output [31:0] res
);


assign res = {n,16'b0};

endmodule
*/

/* Code of memoryDecoder:
module memoryDecoder(
    input [31:0] vAddr,
    input mW,
    input mR,
    output reg [12:0] pAd,
    output reg[2:0] mE,
    output reg[1:0] mB,
    output reg iAd
);

parameter [31:0] startg=32'h10010000;
parameter [31:0] endg=32'h10011000;
parameter [31:0] starts=32'h7FFFEFFC;
parameter [31:0] ends=32'h7FFFFFFC;
parameter [31:0] startvga=32'h0000B800;
parameter [31:0] endvga = 32'h0000CABF;
parameter [31:0] startio = 32'hffff0000;
parameter [31:0] endio = 32'hffff000f;
reg [31:0] temp;

always @(*)

if(mW | mR) 
begin
    if(vAddr>= startg & vAddr<endg)begin
        temp = vAddr - 32'h10010000;
	    pAd = temp;
        iAd = 1'b0;
        mE = 3'b001; //enable datamemory
        mB = 2'b00; //accediendo datamemory
    end else if(vAddr >= starts & vAddr<ends)begin
	temp= vAddr - 32'h7fffdffc;
     	pAd = temp;
        iAd = 1'b0;
        mE = 3'b001;//enable data memory
        mB = 2'b00;//accediendo datamemory
    end else if(vAddr>=startvga & vAddr<=endvga)begin
        pAd = vAddr[12:0] - 32'h0000B800;
        iAd = 1'b0;
        mE = 3'b010;//enable vga
        mB = 2'd1;//accediendo vga
    end else if(vAddr>=startio & vAddr<=endio)begin
        temp = vAddr - 32'hFFFF0000;
        pAd = temp;
        iAd = 1'b0;
        mE = 3'b100;//enable I/O
        mB = 2'b10;//accediendio I/O
    end else begin
        pAd = 13'd0;
        iAd = 1'b1;
        mE = 3'b000;
        mB = 2'b00;
    end
end

endmodule
*/

/* Code of MemoryWDataEncoder:
module MemoryWDataEncoder(
    input [31:0] inD,
    input [1:0]ofs,
    input iwe,
    input [1:0] ds,
    output reg[31:0] oD,
    output reg[3:0] owe
);

always @(*)
if(iwe)
begin
  case (ds)
        2'b00: //Word
        begin
            owe=4'b1111;
            oD = inD;
        end
        2'b01: //Half-Word
        begin
            case (ofs)
              2'b00:
              begin
                owe=4'b0011;
                oD=inD<<16;
              end
              2'b01:
              begin
                owe=4'b0011;
                oD=inD<<16;
              end
              2'b10:
              begin
                owe=4'b1100;
                oD={16'b0,inD[15:0]};
              end
              2'b11:
              begin
                owe=4'b1100;
                oD={16'b0,inD[15:0]};
              end
            endcase
        end
        2'b10: //Byte
        begin
            case(ofs)
              2'b00:
              begin
                owe=4'b0001;
                oD=inD<<24;
              end
              2'b01:
              begin
                owe=4'b0010;
                oD={8'b0,inD[7:0],16'b0};
              end
              2'b10:
              begin
                owe=4'b0100;
                oD={16'b0,inD[7:0],8'b0};
              end
              2'b11:
              begin
                owe=4'b1000;
                oD={24'b0,inD[7:0]};
              end
            endcase
        end
    default: 
        begin
        owe=4'bx;
        oD=31'bx;
        end
  endcase
end else begin
    owe=4'b0000;
    oD=31'b0;
end

endmodule
*/

/* Code of alu:
module alu(
	input[31:0] a,
	input[31:0] b,
	input[3:0] op,
	output reg[31:0] r,
	output isZ
);

assign isZ = r == 32'd0;

always@(*)
begin
	case(op)
		4'd0: r = a + b;
		4'd1: r = a - b;
		4'd2: r = a & b;
		4'd3: r = a | b;
		4'd4: r = {31'd0, $signed(a) < $signed(b)};
        	4'd5: r = a << b;
        	4'd6: r = a >> b;
        	4'd7: r = $signed(a) >>> b;
		4'd8: r = a ^ b;
		4'd9: r = {31'd0, a<b};
		default: r = 32'dX;
	endcase
end

endmodule
*/

/* Code of DataMem:
module DataMem(
    input clk, //! Clock input
    input en, //! Enable
    input [3:0] we, //! Per byte write enable
    input [10:0] addr, //! Address
    input [31:0] wd, //! Write data
    output [31:0] rd, //! Read data
    output [31:0] w
);
 
    reg [31:0] memory[0:2047];
    assign w = memory[0];
    assign rd = en? memory[addr] : 32'hz;


    always @(posedge clk)
    begin
        if (en) begin
            if (we[3]) memory[addr][7:0] <= wd[7:0];
            if (we[2]) memory[addr][15:8] <= wd[15:8];
            if (we[1]) memory[addr][23:16] <= wd[23:16];
            if (we[0]) memory[addr][31:24] <= wd[31:24];
        end
    end
 
`ifndef DIGITAL
    initial begin
        $readmemh("/home/alexander/Documents/Organizacion de Computadoras/MIPS32SOC_Part1_Template/vga_kpad_data.mif", memory, 0, 1023);
    end
`endif 
endmodule
*/

/* Code of VGA80X30Sim:
/home/alexander/Documents/VGA80X30Sim/VGA80X30Sim
*/

/* Code of iomemory:
module iomemory(
    input en,
    input [10:0] addr,
    input [7:0] keypad,
    input [31:0] mscounter,
    output reg[31:0] rd    
);

always @(*) begin
    if(en)
    begin
        if(addr==11'd1)
            rd = {keypad,24'b0};
        else if(addr==11'd2)
            rd = {mscounter};
        else
            rd = 32'b0;
    end
end

endmodule
*/

/* Code of MemoryRDataDecoder:
module MemoryRDataDecoder(
    input [31:0] inD,
    input [1:0] ofs,
    input bitX,
    input [1:0] ds,
    output reg[31:0] oD
);

always @(*)
    case (ds)
      2'b00://Word
      begin
        oD=inD;
      end
      2'b01://Half-Word
      begin
        case (ofs)
          2'b00:
              begin
                if(bitX) begin//do signExtend
                  oD={ {16{inD[31]}},inD[31:16]};
                end else begin
                  oD={16'b0,inD[31:16]};
                end
              end
              2'b01:
              begin
                if(bitX) begin//do signExtend
                  oD={ {16{inD[31]}},inD[31:16]};
                end else begin
                  oD={16'b0,inD[31:16]};
                end
              end
              2'b10:
              begin
                if(bitX) begin
                oD={ {16{inD[15]}},inD[15:0]};
                end else begin
                oD={16'b0,inD[15:0]};
                end
              end
              2'b11:
              begin
                if(bitX) begin
                oD={ {16{inD[15]}},inD[15:0]};
                end else begin
                oD={16'b0,inD[15:0]};
                end
              end
        endcase
      end 
      2'b10://Byte
      begin
        case (ofs)
          2'b00:
              begin
                if(bitX) begin//do signExtend
                  oD={ {24{inD[31]}} ,inD[31:24]};
                end else begin
                  oD={24'b0,inD[31:24]};
                end
              end
              2'b01:
              begin
                if(bitX) begin//do signExtend
                  oD={ {24{inD[23]}},inD[23:16]};
                end else begin
                  oD={24'b0,inD[23:16]};
                end
              end
              2'b10:
              begin
                if(bitX) begin//do signExtend
                  oD={ {24{inD[15]}},inD[15:8]};
                end else begin
                  oD={24'b0,inD[15:8]};
                end
              end
              2'b11:
              begin
                if(bitX) begin//do signExtend
                  oD={ {24{inD[7]}},inD[7:0]};
                end else begin
                  oD={24'b0,inD[7:0]};
                end
              end
        endcase
      end
      default: 
        oD=31'b0;
    endcase
endmodule
*/
