// Digital circuit testBrachResolver.dig as structural Verilog
module testBrachResolver (
  input  beq,
  input  bne,
  input  bgez,
  input  bgtz,
  input  blez,
  input  bltz,
  input  zero,
  input  sign,
  output BranchTaken
);

  branchresolver #(.applicationType("IVERILOG")) u_branchresolver (
    .beq(beq), .bne(bne), .bgez(bgez), .bgtz(bgtz), .blez(blez), .bltz(bltz), .zero(zero), .sign(sign),
    .bt(BranchTaken));
endmodule

/* Code of branchresolver:
module branchresolver(
    input beq,
    input bne,
    input bgez,
    input bgtz,
    input blez,
    input bltz,
    input zero,
    input sign,
    output reg bt
);

always @(*)
begin
    if(beq & zero)
        bt=1'b1;
    else if(bne & !zero)
        bt=1'b1;
    else if(bgez & sign==1'b0)
        bt=1'b1;
    else if(bgtz & sign==1'b0 & zero==1'b0)
        bt=1'b1;
    else if(blez & (sign==1'b1 | zero==1'b0))
        bt=1'b1;
    else if(bltz & sign==1'b1)
        bt=1'b1;
    else
        bt=1'b0;
    
end

endmodule
*/
