// Digital circuit testLui.dig as structural Verilog
module testLui (
  input  [15:0] in_1
);

  wire [31:0] u_lui_res;

  lui #(.applicationType("IVERILOG")) u_lui (.n(in_1), .res(u_lui_res));
  // Probe on u_lui_res
  // Probe on u_lui_res
endmodule

/* Code of lui:
module lui(
    input [15:0] n,
    output [31:0] res
);


assign res = {n,16'b0};

endmodule
*/
