// Digital circuit testMemDecoder.dig as structural Verilog
module testMemDecoder (
  input  [31:0] vAddr,
  input  mWrite,
  input  mRead,
  output [12:0] pAddr,
  output [2:0] mEnab,
  output [1:0] mBank,
  output iAddr
);

  memoryDecoder #(.applicationType("IVERILOG")) u_memoryDecoder (
    .vAddr(vAddr), .mW(mWrite), .mR(mRead), .pAd(pAddr), .mE(mEnab), .mB(mBank), .iAd(iAddr));
endmodule

/* Test case:
vAddr       mWrite mRead pAddr      mEnab mBank iAddr
# Start of Data Memory
0x10010000  0     1     0x00000000  1     0     0   
0x10010001  0     1     0x00000001  1     0     0   
0x10010002  0     1     0x00000002  1     0     0   
0x10010003  0     1     0x00000003  1     0     0   
0x10010000  1     0     0x00000000  1     0     0   
0x10010001  1     0     0x00000001  1     0     0   
0x10010002  1     0     0x00000002  1     0     0   
0x10010003  1     0     0x00000003  1     0     0   
# *** If the address is invalid MemEnable must be 0
0x1000FFFF  1     0     X           0     X     1
0x1000FFFF  0     1     X           0     X     1
0x10011000  1     0     X           0     X     1
0x10011000  0     1     X           0     X     1
# *** ---------------------------------------------
0x10010FFF  0     1     0x00000FFF  1     0     0   
0x10010FFF  1     0     0x00000FFF  1     0     0   
# End of Data Memory
#================================================
# Start of Stack
0x7FFFEFFC  0     1     0x00001000  1     0     0   
0x7FFFEFFD  0     1     0x00001001  1     0     0   
0x7FFFEFFE  0     1     0x00001002  1     0     0   
0x7FFFEFFF  0     1     0x00001003  1     0     0   
0x7FFFEFFC  1     0     0x00001000  1     0     0   
0x7FFFEFFD  1     0     0x00001001  1     0     0   
0x7FFFEFFE  1     0     0x00001002  1     0     0   
0x7FFFEFFF  1     0     0x00001003  1     0     0   
# *** If the address is invalid MemEnable must be 0
0x7FFFEFFB  1     0     X           0     X     1
0x7FFFEFFB  0     1     X           0     X     1
0x7FFFFFFC  1     0     X           0     X     1
0x7FFFFFFC  0     1     X           0     X     1
# *** ---------------------------------------------
0x7FFFFFFB  0     1     0x00001FFF  1     0     0   
0x7FFFFFFB  1     0     0x00001FFF  1     0     0   
# End of Stack
#================================================
# Start of VGA memory
0x0000B800  0     1     0x00000000  2     1     0   
0x0000B801  0     1     0x00000001  2     1     0   
0x0000B802  0     1     0x00000002  2     1     0   
0x0000B803  0     1     0x00000003  2     1     0   
0x0000B800  1     0     0x00000000  2     1     0   
0x0000B801  1     0     0x00000001  2     1     0   
0x0000B802  1     0     0x00000002  2     1     0   
0x0000B803  1     0     0x00000003  2     1     0   
# *** If the address is invalid MemEnable must be 0
0x0000B7FF  1     0     X           0     X     1
0x0000B7FF  0     1     X           0     X     1
0x0000CAC0  1     0     X           0     X     1
0x0000CAC0  0     1     X           0     X     1
# *** ---------------------------------------------
0x0000CABF  0     1     0x000012BF  2     1     0   
0x0000CABF  1     0     0x000012BF  2     1     0   
# End of VGA memory
#================================================
# Start of I/O memory
0xFFFF0000  0     1     0x00000000  4     2     0   
0xFFFF0001  0     1     0x00000001  4     2     0   
0xFFFF0002  0     1     0x00000002  4     2     0   
0xFFFF0003  0     1     0x00000003  4     2     0   
0xFFFF0000  1     0     0x00000000  4     2     0   
0xFFFF0001  1     0     0x00000001  4     2     0   
0xFFFF0002  1     0     0x00000002  4     2     0   
0xFFFF0003  1     0     0x00000003  4     2     0   
# *** If the address is invalid MemEnable must be 0
0xFFFEFFFF  1     0     X           0     X     1
0xFFFEFFFF  0     1     X           0     X     1
0xFFFF0010  1     0     X           0     X     1
0xFFFF0010  0     1     X           0     X     1
# *** ---------------------------------------------
0xFFFF000F  0     1     0x0000000F  4     2     0   
0xFFFF000F  1     0     0x0000000F  4     2     0   
# End of I/O memory
#================================================
*/

/* Code of memoryDecoder:
module memoryDecoder(
    input [31:0] vAddr,
    input mW,
    input mR,
    output reg [12:0] pAd,
    output reg[2:0] mE,
    output reg[1:0] mB,
    output reg iAd
);

parameter [31:0] startg=32'h10010000;
parameter [31:0] endg=32'h10011000;
parameter [31:0] starts=32'h7FFFEFFC;
parameter [31:0] ends=32'h7FFFFFFC;
parameter [31:0] startvga=32'hb800;
parameter [31:0] endvga = 32'hcabf;
parameter [31:0] startio = 32'hffff0000;
parameter [31:0] endio = 32'hffff000f;
reg [31:0] temp;

always @(*)

if(mW | mR) 
begin
    if(vAddr>= startg & vAddr<endg)begin
        temp = vAddr - 32'h10010000;
	    pAd = temp;
        iAd = 1'b0;
        mE = 3'b001; //enable datamemory
        mB = 2'b00; //accediendo datamemory
    end else if(vAddr >= starts & vAddr<ends)begin
	temp= vAddr - 32'h7fffdffc;
     	pAd = temp;
        iAd = 1'b0;
        mE = 3'b001;//enable data memory
        mB = 2'b00;//accediendo datamemory
    end else if(vAddr>=startvga & vAddr<=endvga)begin
        temp = vAddr - 32'hb800;
        pAd = temp;
        iAd = 1'b0;
        mE = 3'b010;//enable vga
        mB = 2'b01;//accediendo vga
    end else if(vAddr>=startio & vAddr<=endio)begin
        temp = vAddr - 32'hFFFF0000;
        pAd = temp;
        iAd = 1'b0;
        mE = 3'b100;//enable I/O
        mB = 2'b10;//accediendio I/O
    end else begin
        pAd = 13'd0;
        iAd = 1'b1;
        mE = 3'b000;
        mB = 2'b00;
    end
end

endmodule
*/
