// Digital circuit testMemoryRDataDecoder.dig as structural Verilog
module testMemoryRDataDecoder (
  input  [31:0] dIn,
  input  [1:0] offset,
  input  dExt,
  input  [1:0] dSize,
  output [31:0] dOut
);

  MemoryRDataDecoder #(.applicationType("IVERILOG")) u_MemoryRDataDecoder (
    .inD(dIn), .ofs(offset), .bitX(dExt), .ds(dSize), .oD(dOut));
endmodule

/* Test case:
dIn          offset  dExt    dSize       dOut

# Word access test
0xaabbccdd   0       0       0           0xaabbccdd
0xaabbccdd   1       0       0           0xaabbccdd
0xaabbccdd   2       0       0           0xaabbccdd
0xaabbccdd   3       0       0           0xaabbccdd
0xaabbccdd   0       1       0           0xaabbccdd
0xaabbccdd   1       1       0           0xaabbccdd
0xaabbccdd   2       1       0           0xaabbccdd
0xaabbccdd   3       1       0           0xaabbccdd

# Half Word tests
0xaabbccdd   0       0       1           0x0000aabb
0xaabbccdd   0       1       1           0xffffaabb
0xaabbccdd   1       0       1           0x0000aabb
0xaabbccdd   1       1       1           0xffffaabb
0xaabbccdd   2       0       1           0x0000ccdd
0xaabbccdd   2       1       1           0xffffccdd
0xaabbccdd   3       0       1           0x0000ccdd
0xaabbccdd   3       1       1           0xffffccdd

# Byte access tests          
0xaabbccdd   0       0       2           0x000000aa
0xaabbccdd   1       0       2           0x000000bb
0xaabbccdd   2       0       2           0x000000cc
0xaabbccdd   3       0       2           0x000000dd
0xaabbccdd   0       1       2           0xffffffaa
0xaabbccdd   1       1       2           0xffffffbb
0xaabbccdd   2       1       2           0xffffffcc
0xaabbccdd   3       1       2           0xffffffdd  
*/

/* Code of MemoryRDataDecoder:
module MemoryRDataDecoder(
    input [31:0] inD,
    input [1:0] ofs,
    input bitX,
    input [1:0] ds,
    output reg[31:0] oD
);

always @(*)
    case (ds)
      2'b00://Word
      begin
        oD=inD;
      end
      2'b01://Half-Word
      begin
        case (ofs)
          2'b00:
              begin
                if(bitX) begin//do signExtend
                  oD={ {16{inD[31]}},inD[31:16]};
                end else begin
                  oD={16'b0,inD[31:16]};
                end
              end
              2'b01:
              begin
                if(bitX) begin//do signExtend
                  oD={ {16{inD[31]}},inD[31:16]};
                end else begin
                  oD={16'b0,inD[31:16]};
                end
              end
              2'b10:
              begin
                if(bitX) begin
                oD={ {16{inD[15]}},inD[15:0]};
                end else begin
                oD={16'b0,inD[15:0]};
                end
              end
              2'b11:
              begin
                if(bitX) begin
                oD={ {16{inD[15]}},inD[15:0]};
                end else begin
                oD={16'b0,inD[15:0]};
                end
              end
        endcase
      end 
      2'b10://Byte
      begin
        case (ofs)
          2'b00:
              begin
                if(bitX) begin//do signExtend
                  oD={ {24{inD[31]}} ,inD[31:24]};
                end else begin
                  oD={24'b0,inD[31:24]};
                end
              end
              2'b01:
              begin
                if(bitX) begin//do signExtend
                  oD={ {24{inD[23]}},inD[23:16]};
                end else begin
                  oD={24'b0,inD[23:16]};
                end
              end
              2'b10:
              begin
                if(bitX) begin//do signExtend
                  oD={ {24{inD[15]}},inD[15:8]};
                end else begin
                  oD={24'b0,inD[15:8]};
                end
              end
              2'b11:
              begin
                if(bitX) begin//do signExtend
                  oD={ {24{inD[7]}},inD[7:0]};
                end else begin
                  oD={24'b0,inD[7:0]};
                end
              end
        endcase
      end
      default: 
        oD=31'b0;
    endcase
endmodule
*/
