// Digital circuit testZeroExtension.dig as structural Verilog
module testZeroExtension (
  input  [15:0] in_1
);

  wire [31:0] u_zeroExtension_res;

  zeroExtension #(.applicationType("IVERILOG")) u_zeroExtension (.n(in_1), .res(u_zeroExtension_res));
  // Probe on u_zeroExtension_res
  // Probe on u_zeroExtension_res
endmodule

/* Code of zeroExtension:
module zeroExtension(
    input [15:0] n,
    output [31:0] res
);

assign res = {16'b0,n};

endmodule
*/
